// Logisim project adders.circ as structural Verilog: 2 circuits, main circuit halfadder_2in_1bit
module halfadder_2in_1bit (
  input  A,
  input  B,
  output S,
  output R
);

  xor xor_1 (S, A, B);
  and and_1 (R, A, B);
endmodule

module fulladder_2in_1bit (
  input  A,
  input  B,
  input  Rin,
  output S,
  output Rout
);

  wire and_1_out, and_2_out, xor_1_out;

  xor xor_1 (xor_1_out, A, B);
  and and_1 (and_1_out, A, B);
  xor xor_2 (S, xor_1_out, Rin);
  or or_1 (Rout, and_1_out, and_2_out);
  and and_2 (and_2_out, Rin, xor_1_out);
endmodule
