// Logisim project decoders.circ as structural Verilog: 1 circuit, main circuit decoder_2in
module decoder_2in (
  input  A,
  input  B,
  output D1,
  output D2,
  output D3,
  output D4
);

  and and_1 (D1, ~A, ~B);  // AND_Gate
  and and_2 (D2, ~A, B);  // AND_Gate
  and and_3 (D3, A, ~B);  // AND_Gate
  and and_4 (D4, A, B);

  // Notes on the sheet:
  //   DECODER
endmodule
