// Logisim project multiplexers.circ as structural Verilog: 1 circuit, main circuit multiplexer_4in
module multiplexer_4in (
  input  A,
  input  B,
  input  C,
  input  D,
  input  D1,
  input  D2,
  output M
);

  wire and_1_out, and_2_out, and_3_out, and_4_out, decoder_2in_1_d1, decoder_2in_1_d2, decoder_2in_1_d3,
       decoder_2in_1_d4;

  decoder_2in decoder_2in_1 (
    .A(D1), .B(D2), .D1(decoder_2in_1_d1), .D2(decoder_2in_1_d2), .D3(decoder_2in_1_d3), .D4(decoder_2in_1_d4));
  and and_1 (and_1_out, decoder_2in_1_d1, A);
  and and_2 (and_2_out, decoder_2in_1_d2, B);
  and and_3 (and_3_out, decoder_2in_1_d3, C);
  and and_4 (and_4_out, decoder_2in_1_d4, D);
  or or_1 (M, and_1_out, and_2_out, and_3_out, and_4_out);

  // Notes on the sheet:
  //   DECODER
endmodule
