// Logisim project multipliers.circ as structural Verilog: 1 circuit, main circuit main
module main (
  input  [3:0] NUMBER,
  input  [3:0] MULTIPLIER,
  output out_3,
  output out_4,
  output out_5,
  output out_6,
  output out_7,
  output out_8,
  output out_9,
  output out_10
);

  wire and_2_out, and_3_out, and_4_out, and_5_out, and_6_out, and_7_out, and_8_out, and_9_out, and_10_out,
       and_11_out, and_12_out, and_13_out, and_14_out, and_15_out, and_16_out, fulladder_2in_1bit_1_rout,
       fulladder_2in_1bit_1_s, fulladder_2in_1bit_2_rout, fulladder_2in_1bit_2_s, fulladder_2in_1bit_3_rout,
       fulladder_2in_1bit_3_s, fulladder_2in_1bit_4_rout, fulladder_2in_1bit_4_s, fulladder_2in_1bit_5_rout,
       fulladder_2in_1bit_5_s, fulladder_2in_1bit_6_rout, fulladder_2in_1bit_6_s, halfadder_2in_1bit_1_r,
       halfadder_2in_1bit_3_r, halfadder_2in_1bit_5_r;

  and and_1 (out_3, MULTIPLIER[0], NUMBER[0]);
  and and_2 (and_2_out, MULTIPLIER[1], NUMBER[0]);
  and and_3 (and_3_out, MULTIPLIER[0], NUMBER[1]);
  and and_4 (and_4_out, MULTIPLIER[1], NUMBER[1]);
  and and_5 (and_5_out, MULTIPLIER[0], NUMBER[2]);
  and and_6 (and_6_out, MULTIPLIER[1], NUMBER[2]);
  and and_7 (and_7_out, MULTIPLIER[0], NUMBER[3]);
  and and_8 (and_8_out, MULTIPLIER[1], NUMBER[3]);
  and and_9 (and_9_out, MULTIPLIER[2], NUMBER[0]);
  and and_10 (and_10_out, MULTIPLIER[3], NUMBER[0]);
  and and_11 (and_11_out, MULTIPLIER[2], NUMBER[1]);
  and and_12 (and_12_out, MULTIPLIER[3], NUMBER[1]);
  and and_13 (and_13_out, MULTIPLIER[2], NUMBER[2]);
  and and_14 (and_14_out, MULTIPLIER[3], NUMBER[2]);
  and and_15 (and_15_out, MULTIPLIER[2], NUMBER[3]);
  and and_16 (and_16_out, MULTIPLIER[3], NUMBER[3]);
  halfadder_2in_1bit halfadder_2in_1bit_1 (.A(and_2_out), .B(and_3_out), .S(out_4), .R(halfadder_2in_1bit_1_r));
  fulladder_2in_1bit fulladder_2in_1bit_1 (
    .A(halfadder_2in_1bit_1_r), .B(and_4_out), .Rin(and_5_out), .S(fulladder_2in_1bit_1_s),
    .Rout(fulladder_2in_1bit_1_rout));
  fulladder_2in_1bit fulladder_2in_1bit_2 (
    .A(fulladder_2in_1bit_1_rout), .B(and_6_out), .Rin(and_7_out), .S(fulladder_2in_1bit_2_s),
    .Rout(fulladder_2in_1bit_2_rout));
  fulladder_2in_1bit fulladder_2in_1bit_3 (
    .A(fulladder_2in_1bit_2_rout), .B(and_13_out), .Rin(and_8_out), .S(fulladder_2in_1bit_3_s),
    .Rout(fulladder_2in_1bit_3_rout));
  fulladder_2in_1bit fulladder_2in_1bit_4 (
    .A(fulladder_2in_1bit_3_rout), .B(and_14_out), .Rin(and_15_out), .S(fulladder_2in_1bit_4_s),
    .Rout(fulladder_2in_1bit_4_rout));
  halfadder_2in_1bit halfadder_2in_1bit_2 (.A(and_16_out), .B(fulladder_2in_1bit_4_rout), .S(out_9), .R(out_10));
  halfadder_2in_1bit halfadder_2in_1bit_3 (
    .A(and_9_out), .B(fulladder_2in_1bit_1_s), .S(out_5), .R(halfadder_2in_1bit_3_r));
  fulladder_2in_1bit fulladder_2in_1bit_5 (
    .A(halfadder_2in_1bit_3_r), .B(and_11_out), .Rin(fulladder_2in_1bit_2_s), .S(fulladder_2in_1bit_5_s),
    .Rout(fulladder_2in_1bit_5_rout));
  fulladder_2in_1bit fulladder_2in_1bit_6 (
    .A(fulladder_2in_1bit_5_rout), .B(and_12_out), .Rin(fulladder_2in_1bit_3_s), .S(fulladder_2in_1bit_6_s),
    .Rout(fulladder_2in_1bit_6_rout));
  halfadder_2in_1bit halfadder_2in_1bit_4 (
    .A(fulladder_2in_1bit_4_s), .B(fulladder_2in_1bit_6_rout), .S(out_8));  // open: R
  halfadder_2in_1bit halfadder_2in_1bit_5 (
    .A(and_10_out), .B(fulladder_2in_1bit_5_s), .S(out_6), .R(halfadder_2in_1bit_5_r));
  halfadder_2in_1bit halfadder_2in_1bit_6 (
    .A(fulladder_2in_1bit_6_s), .B(halfadder_2in_1bit_5_r), .S(out_7));  // open: R
endmodule
