// Logisim project progetto.circ as structural Verilog: 1 circuit, main circuit main
module main (
  input  [2:0] in_1,
  input  [2:0] in_2,
  input  in_3,
  input  [2:0] X0,
  input  [2:0] X1,
  input  [2:0] X2,
  input  [2:0] X3,
  input  [2:0] X4,
  input  [2:0] X5
);

  wire [2:0] adder_1_out, adder_2_out, adder_3_out, adder_4_out, adder_5_out, multiplier_1_out,
       multiplier_2_out, multiplier_3_out, multiplier_4_out, multiplier_5_out;
  wire [4:0] demultiplexer_1_out0, demultiplexer_2_out0, demultiplexer_3_out0, demultiplexer_4_out0,
       demultiplexer_5_out0;

  Multiplier #(.width(3)) multiplier_1 (.a(in_2), .b(X0), .out(multiplier_1_out));  // open: cin, cout
  Multiplier #(.width(3)) multiplier_2 (.a(in_2), .b(X1), .out(multiplier_2_out));  // open: cin, cout
  Multiplier #(.width(3)) multiplier_3 (.a(in_2), .b(X2), .out(multiplier_3_out));  // open: cin, cout
  Multiplier #(.width(3)) multiplier_4 (.a(in_2), .b(X3), .out(multiplier_4_out));  // open: cin, cout
  Multiplier #(.width(3)) multiplier_5 (.a(in_2), .b(X4), .out(multiplier_5_out));  // open: cin, cout
  Adder #(.width(3)) adder_1 (.a(multiplier_1_out), .b(in_1), .out(adder_1_out));  // open: cin, cout
  Adder #(.width(3)) adder_2 (.a(multiplier_2_out), .b(in_1), .out(adder_2_out));  // open: cin, cout
  Adder #(.width(3)) adder_3 (.a(multiplier_3_out), .b(in_1), .out(adder_3_out));  // open: cin, cout
  Adder #(.width(3)) adder_4 (.a(multiplier_4_out), .b(in_1), .out(adder_4_out));  // open: cin, cout
  Adder #(.width(3)) adder_5 (.a(multiplier_5_out), .b(in_1), .out(adder_5_out));  // open: cin, cout
  Demultiplexer #(.select(3)) demultiplexer_1 (
    .out0(demultiplexer_1_out0[0]), .out1(demultiplexer_1_out0[1]), .out2(demultiplexer_1_out0[2]),
    .out3(demultiplexer_1_out0[3]), .out4(demultiplexer_1_out0[4]), .in(in_3), .sel(adder_1_out));  // open: out5, out6, out7, en
  Demultiplexer #(.select(3)) demultiplexer_2 (
    .out0(demultiplexer_2_out0[0]), .out1(demultiplexer_2_out0[1]), .out2(demultiplexer_2_out0[2]),
    .out3(demultiplexer_2_out0[3]), .out4(demultiplexer_2_out0[4]), .in(in_3), .sel(adder_2_out));  // open: out5, out6, out7, en
  Demultiplexer #(.select(3)) demultiplexer_3 (
    .out0(demultiplexer_3_out0[0]), .out1(demultiplexer_3_out0[1]), .out2(demultiplexer_3_out0[2]),
    .out3(demultiplexer_3_out0[3]), .out4(demultiplexer_3_out0[4]), .in(in_3), .sel(adder_3_out));  // open: out5, out6, out7, en
  Demultiplexer #(.select(3)) demultiplexer_4 (
    .out0(demultiplexer_4_out0[0]), .out1(demultiplexer_4_out0[1]), .out2(demultiplexer_4_out0[2]),
    .out3(demultiplexer_4_out0[3]), .out4(demultiplexer_4_out0[4]), .in(in_3), .sel(adder_4_out));  // open: out5, out6, out7, en
  Demultiplexer #(.select(3)) demultiplexer_5 (
    .out0(demultiplexer_5_out0[0]), .out1(demultiplexer_5_out0[1]), .out2(demultiplexer_5_out0[2]),
    .out3(demultiplexer_5_out0[3]), .out4(demultiplexer_5_out0[4]), .in(in_3), .sel(adder_5_out));  // open: out5, out6, out7, en
  DotMatrix #(.matrixrows(5)) dotmatrix_1 (
    .col0(demultiplexer_1_out0), .col1(demultiplexer_2_out0), .col2(demultiplexer_3_out0),
    .col3(demultiplexer_4_out0), .col4(demultiplexer_5_out0));
endmodule
