// Logisim project deps.circ as structural Verilog: 17 circuits, main circuit demo
module demo (
  output [3:0] out_1,
  output [1:0] out_2,
  output [3:0] out_3,
  output [3:0] out_4,
  output [3:0] out_5,
  output [3:0] out_6,
  output [3:0] out_7,
  output [3:0] out_8,
  output [3:0] out_9,
  output [3:0] out_10
);

  wire _0_out, _1_out, _2_out, _3_out, _4_out, _5_out, _6_out, _7_out, _8_out, _9_out, Azzera, Back,
       button_2_out, button_out, canc, Clock, keypad_1_clicked, load, not_1_out, not_2_out, of, OK_out,
       op_out, or_1_out, or_2_out, or_3_out, or_4_out, or_5_out, or_6_out, or_7_out, or_8_out, or_9_out,
       Reset, save;
  wire [1:0] counter_2_q, multiplexer_4_out, op_code;
  wire [3:0] keypad_1_b0, multiplexer_1_out, multiplexer_2_out, multiplexer_3_out;
  wire [4:0] calcolo_1_out_5, X, Y;
  wire [31:0] draw_memory_1_out_35, draw_memory_1_out_36, draw_memory_1_out_37, draw_memory_1_out_38,
       draw_memory_1_out_39, draw_memory_1_out_40, draw_memory_1_out_41, draw_memory_1_out_42,
       draw_memory_1_out_43, draw_memory_1_out_44, draw_memory_1_out_45, draw_memory_1_out_46,
       draw_memory_1_out_47, draw_memory_1_out_48, draw_memory_1_out_49, draw_memory_1_out_50,
       draw_memory_1_out_51, draw_memory_1_out_52, draw_memory_1_out_53, draw_memory_1_out_54,
       draw_memory_1_out_55, draw_memory_1_out_56, draw_memory_1_out_57, draw_memory_1_out_58,
       draw_memory_1_out_59, draw_memory_1_out_60, draw_memory_1_out_61, draw_memory_1_out_62,
       draw_memory_1_out_63, draw_memory_1_out_64, draw_memory_1_out_65, draw_memory_1_out_66,
       drawer_1_out_67, drawer_1_out_68, drawer_1_out_69, drawer_1_out_70, drawer_1_out_71, drawer_1_out_72,
       drawer_1_out_73, drawer_1_out_74, drawer_1_out_75, drawer_1_out_76, drawer_1_out_77, drawer_1_out_78,
       drawer_1_out_79, drawer_1_out_80, drawer_1_out_81, drawer_1_out_82, drawer_1_out_83, drawer_1_out_84,
       drawer_1_out_85, drawer_1_out_86, drawer_1_out_87, drawer_1_out_88, drawer_1_out_89, drawer_1_out_90,
       drawer_1_out_91, drawer_1_out_92, drawer_1_out_93, drawer_1_out_94, drawer_1_out_95, drawer_1_out_96,
       drawer_1_out_97, drawer_1_y0_merged, y0, y1, y2, y3, y4, y5, y6, y7, y8, y9, y10, y11, y12, y13, y14,
       y15, y16, y17, y18, y19, y20, y21, y22, y23, y24, y25, y26, y27, y28, y29, y30, y31;

  Button R (.out(Reset));
  Button _7 (.out(_7_out));
  Button _8 (.out(_8_out));
  Button _4 (.out(_4_out));
  Button _5 (.out(_5_out));
  Button _2 (.out(_2_out));
  Button _1 (.out(_1_out));
  Button _0 (.out(_0_out));
  Button u_azzera (.out(Azzera));
  Button OK (.out(OK_out));
  Button button (.out(button_out));
  Button button_2 (.out(button_2_out));
  Button u_save (.out(save));
  Button u_canc (.out(canc));
  Button op (.out(op_out));
  DotMatrix #(.matrixcols(32), .matrixrows(32)) dotmatrix_1 (
    .col0(drawer_1_y0_merged), .col1(drawer_1_out_67), .col2(drawer_1_out_68), .col3(drawer_1_out_69),
    .col4(drawer_1_out_70), .col5(drawer_1_out_71), .col6(drawer_1_out_72), .col7(drawer_1_out_73),
    .col8(drawer_1_out_74), .col9(drawer_1_out_75), .col10(drawer_1_out_76), .col11(drawer_1_out_77),
    .col12(drawer_1_out_78), .col13(drawer_1_out_79), .col14(drawer_1_out_80), .col15(drawer_1_out_81),
    .col16(drawer_1_out_82), .col17(drawer_1_out_83), .col18(drawer_1_out_84), .col19(drawer_1_out_85),
    .col20(drawer_1_out_86), .col21(drawer_1_out_87), .col22(drawer_1_out_88), .col23(drawer_1_out_89),
    .col24(drawer_1_out_90), .col25(drawer_1_out_91), .col26(drawer_1_out_92), .col27(drawer_1_out_93),
    .col28(drawer_1_out_94), .col29(drawer_1_out_95), .col30(drawer_1_out_96), .col31(drawer_1_out_97));
  drawer drawer_1 (
    .y0_saved(draw_memory_1_out_35), .y0(y0), .in_4(draw_memory_1_out_36), .in_5(y1),
    .in_6(draw_memory_1_out_37), .in_7(y2), .in_8(draw_memory_1_out_38), .in_9(y3),
    .in_10(draw_memory_1_out_39), .in_11(y4), .in_12(draw_memory_1_out_40), .in_13(y5),
    .in_14(draw_memory_1_out_41), .in_15(y6), .in_16(draw_memory_1_out_42), .in_17(y7),
    .in_18(draw_memory_1_out_43), .in_19(y8), .in_20(draw_memory_1_out_44), .in_21(y9),
    .in_22(draw_memory_1_out_45), .in_23(y10), .in_24(draw_memory_1_out_46), .in_25(y11),
    .in_26(draw_memory_1_out_47), .in_27(y12), .in_28(draw_memory_1_out_48), .in_29(y13),
    .in_30(draw_memory_1_out_49), .in_31(y14), .in_32(draw_memory_1_out_50), .in_33(y15),
    .in_34(draw_memory_1_out_51), .in_35(y16), .in_36(draw_memory_1_out_52), .in_37(y17),
    .in_38(draw_memory_1_out_53), .in_39(y18), .in_40(draw_memory_1_out_54), .in_41(y19),
    .in_42(draw_memory_1_out_55), .in_43(y20), .in_44(draw_memory_1_out_56), .in_45(y21),
    .in_46(draw_memory_1_out_57), .in_47(y22), .in_48(draw_memory_1_out_58), .in_49(y23),
    .in_50(draw_memory_1_out_59), .in_51(y24), .in_52(draw_memory_1_out_60), .in_53(y25),
    .in_54(draw_memory_1_out_61), .in_55(y26), .in_56(draw_memory_1_out_62), .in_57(y27),
    .in_58(draw_memory_1_out_63), .in_59(y28), .in_60(draw_memory_1_out_64), .in_61(y29),
    .in_62(draw_memory_1_out_65), .in_63(y30), .in_64(draw_memory_1_out_66), .in_65(y31),
    .y0_merged(drawer_1_y0_merged), .out_67(drawer_1_out_67), .out_68(drawer_1_out_68),
    .out_69(drawer_1_out_69), .out_70(drawer_1_out_70), .out_71(drawer_1_out_71), .out_72(drawer_1_out_72),
    .out_73(drawer_1_out_73), .out_74(drawer_1_out_74), .out_75(drawer_1_out_75), .out_76(drawer_1_out_76),
    .out_77(drawer_1_out_77), .out_78(drawer_1_out_78), .out_79(drawer_1_out_79), .out_80(drawer_1_out_80),
    .out_81(drawer_1_out_81), .out_82(drawer_1_out_82), .out_83(drawer_1_out_83), .out_84(drawer_1_out_84),
    .out_85(drawer_1_out_85), .out_86(drawer_1_out_86), .out_87(drawer_1_out_87), .out_88(drawer_1_out_88),
    .out_89(drawer_1_out_89), .out_90(drawer_1_out_90), .out_91(drawer_1_out_91), .out_92(drawer_1_out_92),
    .out_93(drawer_1_out_93), .out_94(drawer_1_out_94), .out_95(drawer_1_out_95), .out_96(drawer_1_out_96),
    .out_97(drawer_1_out_97), .in_1(op_code));
  draw_memory draw_memory_1 (
    .save(save), .reset(or_4_out), .in_3(y0), .in_4(y1), .in_5(y2), .in_6(y3), .in_7(y4), .in_8(y5),
    .in_9(y6), .in_10(y7), .in_11(y8), .in_12(y9), .in_13(y10), .in_14(y11), .in_15(y12), .in_16(y13),
    .in_17(y14), .in_18(y15), .in_19(y16), .in_20(y17), .in_21(y18), .in_22(y19), .in_23(y20), .in_24(y21),
    .in_25(y22), .in_26(y23), .in_27(y24), .in_28(y25), .in_29(y26), .in_30(y27), .in_31(y28), .in_32(y29),
    .in_33(y30), .in_34(y31), .out_35(draw_memory_1_out_35), .out_36(draw_memory_1_out_36),
    .out_37(draw_memory_1_out_37), .out_38(draw_memory_1_out_38), .out_39(draw_memory_1_out_39),
    .out_40(draw_memory_1_out_40), .out_41(draw_memory_1_out_41), .out_42(draw_memory_1_out_42),
    .out_43(draw_memory_1_out_43), .out_44(draw_memory_1_out_44), .out_45(draw_memory_1_out_45),
    .out_46(draw_memory_1_out_46), .out_47(draw_memory_1_out_47), .out_48(draw_memory_1_out_48),
    .out_49(draw_memory_1_out_49), .out_50(draw_memory_1_out_50), .out_51(draw_memory_1_out_51),
    .out_52(draw_memory_1_out_52), .out_53(draw_memory_1_out_53), .out_54(draw_memory_1_out_54),
    .out_55(draw_memory_1_out_55), .out_56(draw_memory_1_out_56), .out_57(draw_memory_1_out_57),
    .out_58(draw_memory_1_out_58), .out_59(draw_memory_1_out_59), .out_60(draw_memory_1_out_60),
    .out_61(draw_memory_1_out_61), .out_62(draw_memory_1_out_62), .out_63(draw_memory_1_out_63),
    .out_64(draw_memory_1_out_64), .out_65(draw_memory_1_out_65), .out_66(draw_memory_1_out_66));
  Button _9 (.out(_9_out));
  Button _6 (.out(_6_out));
  Button _3 (.out(_3_out));
  Button u_back (.out(Back));
  not not_1 (not_1_out, not_2_out);
  or or_1 (or_1_out, OK_out, button_out, button_2_out);
  not not_2 (not_2_out, button_2_out);
  Button u_load (.out(load));
  Counter #(.width(2), .max('h2), .trigger("falling")) counter_1 (
    .Q(op_code), .clk(op_out), .clr(Reset));  // open: load, D, count, carry
  keypad keypad_1 (
    ._0(_0_out), ._1(_1_out), ._3(_3_out), ._2(_2_out), ._5(_5_out), ._4(_4_out), ._7(_7_out), ._6(_6_out),
    .b2_2(keypad_1_b0[2]), .b1(keypad_1_b0[1]), .b0(keypad_1_b0[0]), ._8(_8_out), ._9(_9_out),
    .b2(keypad_1_b0[3]), .clicked(keypad_1_clicked));
  Counter #(.width(2), .max('h2), .ongoal("stay"), .trigger("falling")) counter_2 (
    .load(not_1_out), .count(not_2_out), .Q(counter_2_q), .clk(or_1_out), .clr(or_2_out));  // open: D, carry
  or or_2 (or_2_out, Reset, Azzera, save);
  Multiplexer #(.width(4)) multiplexer_1 (.in0(out_1), .in1(out_8), .out(multiplexer_1_out), .sel(load));  // open: en
  Multiplexer #(.width(4)) multiplexer_2 (.in0(out_3), .in1(out_9), .out(multiplexer_2_out), .sel(load));  // open: en
  Multiplexer #(.width(4)) multiplexer_3 (.in0(out_4), .in1(out_10), .out(multiplexer_3_out), .sel(load));  // open: en
  or or_3 (or_3_out, Azzera, Reset, save);
  Counter #(.width(5), .max('h1f)) u_X (.Q(X), .clk(Clock), .clr(Reset));  // open: load, D, count, carry
  Clock CLK (.out(Clock));
  or or_4 (or_4_out, canc, Reset);
  back_memory back_memory_1 (
    .q(out_7), .back(Back), .out_11(out_4), .out_12(out_2), .select(counter_2_q), .reset(or_6_out),
    .x(out_6), .x_2(out_5), .out_10(out_3), .out_9(out_1), .completo(or_7_out), .ok(or_8_out));
  Multiplexer #(.width(2)) multiplexer_4 (.in0(out_2), .in1(2'b11), .out(multiplexer_4_out), .sel(load));  // open: en
  or or_5 (or_5_out, Back, load);
  memory memory_1 (
    .in_1(keypad_1_b0), .in_2(keypad_1_clicked), .in_3(OK_out), .in_4(counter_2_q), .out_11(out_5),
    .out_12(out_6), .out_13(out_7), .Reset(or_3_out), .back_x_2(multiplexer_1_out),
    .back_select(multiplexer_4_out), .back_save(or_5_out), .back_x(multiplexer_2_out),
    .back_q(multiplexer_3_out));
  xy_selector xy_selector_1 (
    .x(X), .y(Y), .x16_output(y16), .CLK(Clock), .x17_output(y17), .x18_output(y18), .x19_output(y19),
    .x20_output(y20), .x21_output(y21), .x22_output(y22), .x23_output(y23), .x24_output(y24),
    .x25_output(y25), .x26_output(y26), .x27_output(y27), .x28_output(y28), .x29_output(y29),
    .x30_output(y30), .x31_output(y31), .x0_output(y0), .x1_output(y1), .x2_output(y2), .x3_output(y3),
    .x4_output(y4), .x5_output(y5), .x6_output(y6), .x7_output(y7), .x8_output(y8), .x9_output(y9),
    .x10_output(y10), .x11_output(y11), .x12_output(y12), .x13_output(y13), .x14_output(y14),
    .x15_output(y15), .of(of), .Reset(Reset));
  or or_6 (or_6_out, Reset, canc);
  calcolo calcolo_1 (.c_x_2(out_5), .c_x(out_6), .q(out_7), .out_5(calcolo_1_out_5), .x(X), .out_6(of));
  or or_7 (or_7_out, Azzera, load, save);
  or or_8 (or_8_out, OK_out, load, save, Azzera);
  saved_memory saved_memory_1 (
    .x_2(out_5), .x(out_6), .q(out_7), .save(save), .out_6(out_8), .out_7(out_9), .out_8(out_10),
    .reset(or_9_out));
  or or_9 (or_9_out, canc, Reset);
  assign Y = calcolo_1_out_5 & ~{5{of}};  // AND_Gate and_1, 5 bits wide

  // Other names for the same wires on the sheet: q_saved[3:0] = out_10; x_2_saved[3:0] = out_8; x_saved[3:0] = out_9
endmodule

module keypad (
  input  _0,
  input  _1,
  input  _3,
  input  _2,
  input  _5,
  input  _4,
  input  _7,
  input  _6,
  input  _9,
  input  _8,
  output clicked,
  output b2,
  output b2_2,
  output b1,
  output b0
);

  or or_1 (b0, _1, _9, _3, _5, _7);
  or or_2 (b1, _3, _2, _7, _6);
  or or_3 (b2_2, _6, _5, _7, _4);
  or or_4 (b2, _9, _8);
  or or_5 (clicked, _0, b0, b1, b2_2, b2);
endmodule

module memory (
  input  [3:0] in_1,
  input  in_2,
  input  in_3,
  input  [1:0] in_4,
  input  Reset,
  input  [3:0] back_x_2,
  input  [3:0] back_x,
  input  [3:0] back_q,
  input  [1:0] back_select,
  input  back_save,
  output [3:0] out_11,
  output [3:0] out_12,
  output [3:0] out_13
);

  wire demultiplexer_1_out0, demultiplexer_1_out1, demultiplexer_1_out2, demultiplexer_2_out0,
       demultiplexer_2_out1, demultiplexer_2_out2, or_2_out, or_3_out, or_4_out, save0, save1, save2, saveAll;
  wire [3:0] d_ff_1_q, multiplexer_1_out, multiplexer_2_out, multiplexer_3_out;

  D_Flip_Flop d_ff_1 (.clk(in_2), .D(in_1[0]), .Q(d_ff_1_q[0]), .reset(Reset));  // open: Qn, preset, en
  D_Flip_Flop d_ff_2 (.clk(in_2), .D(in_1[1]), .Q(d_ff_1_q[1]), .reset(Reset));  // open: Qn, preset, en
  D_Flip_Flop d_ff_3 (.clk(in_2), .D(in_1[2]), .Q(d_ff_1_q[2]), .reset(Reset));  // open: Qn, preset, en
  D_Flip_Flop d_ff_4 (.clk(in_2), .D(in_1[3]), .Q(d_ff_1_q[3]));  // open: Qn, preset, en, reset
  Multiplexer #(.width(4)) multiplexer_1 (
    .in0(d_ff_1_q), .in1(back_x_2), .out(multiplexer_1_out), .sel(back_save));  // open: en
  Multiplexer #(.width(4)) multiplexer_2 (
    .in0(d_ff_1_q), .in1(back_x), .out(multiplexer_2_out), .sel(back_save));  // open: en
  Multiplexer #(.width(4)) multiplexer_3 (
    .in0(d_ff_1_q), .in1(back_q), .out(multiplexer_3_out), .sel(back_save));  // open: en
  Demultiplexer #(.select(2)) demultiplexer_1 (
    .out0(demultiplexer_1_out0), .out1(demultiplexer_1_out1), .out2(demultiplexer_1_out2), .in(in_3),
    .sel(in_4));  // open: out3, en
  Demultiplexer #(.select(2)) demultiplexer_2 (
    .out0(demultiplexer_2_out0), .out1(demultiplexer_2_out1), .out2(demultiplexer_2_out2), .out3(saveAll),
    .in(back_save), .sel(back_select));  // open: en
  or or_1 (save0, demultiplexer_1_out0, demultiplexer_2_out0);
  Register #(.width(4)) register_1 (.D(multiplexer_1_out), .Q(out_11), .clk(or_2_out), .clr(Reset));  // open: en
  or or_2 (or_2_out, save0, saveAll);
  Register #(.width(4)) register_2 (.D(multiplexer_2_out), .Q(out_12), .clk(or_3_out), .clr(Reset));  // open: en
  or or_3 (or_3_out, save1, saveAll);
  Register #(.width(4)) register_3 (.D(multiplexer_3_out), .Q(out_13), .clk(or_4_out), .clr(Reset));  // open: en
  or or_4 (or_4_out, save2, saveAll);
  or or_5 (save1, demultiplexer_1_out1, demultiplexer_2_out1);
  or or_6 (save2, demultiplexer_1_out2, demultiplexer_2_out2);
endmodule

module calcolo (
  input  [3:0] c_x_2,
  input  [3:0] c_x,
  input  [3:0] q,
  input  [4:0] x,
  output [4:0] out_5,
  output out_6
);

  wire adder_1_cout, adder_2_cout;
  wire [4:0] adder_1_out, multiplier_1_cout, multiplier_1_out, multiplier_2_cout, multiplier_2_out,
       multiplier_3_cout, multiplier_3_out;

  Multiplier #(.width(5)) multiplier_1 (
    .a({1'b0, c_x}), .b(x), .out(multiplier_1_out), .cout(multiplier_1_cout));  // open: cin
  Multiplier #(.width(5)) multiplier_2 (
    .a({1'b0, c_x_2}), .b(x), .out(multiplier_2_out), .cout(multiplier_2_cout));  // open: cin
  Multiplier #(.width(5)) multiplier_3 (
    .a(multiplier_2_out), .b(x), .out(multiplier_3_out), .cout(multiplier_3_cout));  // open: cin
  Adder #(.width(5)) adder_1 (
    .a(multiplier_3_out), .b(multiplier_1_out), .out(adder_1_out), .cout(adder_1_cout));  // open: cin
  Adder #(.width(5)) adder_2 (.a({1'b0, q}), .b(adder_1_out), .out(out_5), .cin(adder_1_cout), .cout(adder_2_cout));
  or or_1 (out_6, adder_1_cout, adder_2_cout, multiplier_3_cout[0], multiplier_3_cout[1], multiplier_3_cout[2], multiplier_3_cout[3], multiplier_3_cout[4], multiplier_1_cout[0], multiplier_1_cout[1], multiplier_1_cout[2], multiplier_1_cout[3], multiplier_1_cout[4], multiplier_2_cout[0], multiplier_2_cout[1], multiplier_2_cout[2], multiplier_2_cout[3], multiplier_2_cout[4]);
endmodule

module xy_selector (
  input  [4:0] x,
  input  [4:0] y,
  input  CLK,
  input  Reset,
  input  of,
  output [31:0] x0_output,
  output [31:0] x16_output,
  output [31:0] x1_output,
  output [31:0] x17_output,
  output [31:0] x2_output,
  output [31:0] x18_output,
  output [31:0] x3_output,
  output [31:0] x19_output,
  output [31:0] x4_output,
  output [31:0] x20_output,
  output [31:0] x5_output,
  output [31:0] x21_output,
  output [31:0] x6_output,
  output [31:0] x22_output,
  output [31:0] x7_output,
  output [31:0] x23_output,
  output [31:0] x8_output,
  output [31:0] x24_output,
  output [31:0] x9_output,
  output [31:0] x25_output,
  output [31:0] x10_output,
  output [31:0] x26_output,
  output [31:0] x11_output,
  output [31:0] x27_output,
  output [31:0] x12_output,
  output [31:0] x28_output,
  output [31:0] x13_output,
  output [31:0] x29_output,
  output [31:0] x14_output,
  output [31:0] x30_output,
  output [31:0] x15_output,
  output [31:0] x31_output
);

  wire and_2_out, and_3_out, and_4_out, and_5_out, and_6_out, and_7_out, and_8_out, and_9_out, and_10_out,
       and_11_out, and_12_out, and_13_out, and_14_out, and_15_out, and_16_out, and_17_out, and_18_out,
       and_19_out, and_20_out, and_21_out, and_22_out, and_23_out, and_24_out, and_25_out, and_26_out,
       and_27_out, and_28_out, and_29_out, and_30_out, and_31_out, and_32_out, and_33_out;
  wire [31:0] y_star, y_t;

  assign y_star = ~{32{of}} & y_t;  // AND_Gate and_1, 32 bits wide
  Decoder #(.select(5)) decoder_1 (
    .out0(y_t[0]), .out1(y_t[1]), .out2(y_t[2]), .out3(y_t[3]), .out4(y_t[4]), .out5(y_t[5]), .out6(y_t[6]),
    .out7(y_t[7]), .out8(y_t[8]), .out9(y_t[9]), .out10(y_t[10]), .out11(y_t[11]), .out12(y_t[12]),
    .out13(y_t[13]), .out14(y_t[14]), .out15(y_t[15]), .out16(y_t[16]), .out17(y_t[17]), .out18(y_t[18]),
    .out19(y_t[19]), .out20(y_t[20]), .out21(y_t[21]), .out22(y_t[22]), .out23(y_t[23]), .out24(y_t[24]),
    .out25(y_t[25]), .out26(y_t[26]), .out27(y_t[27]), .out28(y_t[28]), .out29(y_t[29]), .out30(y_t[30]),
    .out31(y_t[31]), .sel(y));  // open: en
  Register #(.width(32), .trigger("high")) x16 (.D(y_star), .Q(x16_output), .clk(and_2_out), .clr(Reset));  // open: en
  and and_2 (and_2_out, x[4], ~x[3], ~x[2], ~x[1], ~x[0], CLK);  // AND_Gate
  Register #(.width(32), .trigger("high")) x17 (.D(y_star), .Q(x17_output), .clk(and_3_out), .clr(Reset));  // open: en
  and and_3 (and_3_out, x[4], ~x[3], ~x[2], ~x[1], x[0], CLK);  // AND_Gate
  Register #(.width(32), .trigger("high")) x18 (.D(y_star), .Q(x18_output), .clk(and_4_out), .clr(Reset));  // open: en
  and and_4 (and_4_out, x[4], ~x[3], ~x[2], x[1], ~x[0], CLK);  // AND_Gate
  Register #(.width(32), .trigger("high")) x19 (.D(y_star), .Q(x19_output), .clk(and_5_out), .clr(Reset));  // open: en
  and and_5 (and_5_out, x[4], ~x[3], ~x[2], x[1], x[0], CLK);  // AND_Gate
  Register #(.width(32), .trigger("high")) x20 (.D(y_star), .Q(x20_output), .clk(and_6_out), .clr(Reset));  // open: en
  and and_6 (and_6_out, x[4], ~x[3], x[2], ~x[1], ~x[0], CLK);  // AND_Gate
  Register #(.width(32), .trigger("high")) x21 (.D(y_star), .Q(x21_output), .clk(and_7_out), .clr(Reset));  // open: en
  and and_7 (and_7_out, x[4], ~x[3], x[2], ~x[1], x[0], CLK);  // AND_Gate
  Register #(.width(32), .trigger("high")) x22 (.D(y_star), .Q(x22_output), .clk(and_8_out), .clr(Reset));  // open: en
  and and_8 (and_8_out, x[4], ~x[3], x[2], x[1], ~x[0], CLK);  // AND_Gate
  Register #(.width(32), .trigger("high")) x23 (.D(y_star), .Q(x23_output), .clk(and_9_out), .clr(Reset));  // open: en
  and and_9 (and_9_out, x[4], ~x[3], x[2], x[1], x[0], CLK);  // AND_Gate
  Register #(.width(32), .trigger("high")) x24 (.D(y_star), .Q(x24_output), .clk(and_10_out), .clr(Reset));  // open: en
  and and_10 (and_10_out, x[4], x[3], ~x[2], ~x[1], ~x[0], CLK);  // AND_Gate
  Register #(.width(32), .trigger("high")) x25 (.D(y_star), .Q(x25_output), .clk(and_11_out), .clr(Reset));  // open: en
  and and_11 (and_11_out, x[4], x[3], ~x[2], ~x[1], x[0], CLK);  // AND_Gate
  Register #(.width(32), .trigger("high")) x26 (.D(y_star), .Q(x26_output), .clk(and_12_out), .clr(Reset));  // open: en
  and and_12 (and_12_out, x[4], x[3], ~x[2], x[1], ~x[0], CLK);  // AND_Gate
  Register #(.width(32), .trigger("high")) x27 (.D(y_star), .Q(x27_output), .clk(and_13_out), .clr(Reset));  // open: en
  and and_13 (and_13_out, x[4], x[3], ~x[2], x[1], x[0], CLK);  // AND_Gate
  Register #(.width(32), .trigger("high")) x28 (.D(y_star), .Q(x28_output), .clk(and_14_out), .clr(Reset));  // open: en
  and and_14 (and_14_out, x[4], x[3], x[2], ~x[1], ~x[0], CLK);  // AND_Gate
  Register #(.width(32), .trigger("high")) x29 (.D(y_star), .Q(x29_output), .clk(and_15_out), .clr(Reset));  // open: en
  and and_15 (and_15_out, x[4], x[3], x[2], ~x[1], x[0], CLK);  // AND_Gate
  Register #(.width(32), .trigger("high")) x30 (.D(y_star), .Q(x30_output), .clk(and_16_out), .clr(Reset));  // open: en
  and and_16 (and_16_out, x[4], x[3], x[2], x[1], ~x[0], CLK);  // AND_Gate
  Register #(.width(32), .trigger("high")) x31 (.D(y_star), .Q(x31_output), .clk(and_17_out), .clr(Reset));  // open: en
  and and_17 (and_17_out, x[4], x[3], x[2], x[1], x[0], CLK);
  Register #(.width(32), .trigger("high")) x0 (.D(y_star), .Q(x0_output), .clk(and_18_out), .clr(Reset));  // open: en
  and and_18 (and_18_out, ~x[4], ~x[3], ~x[2], ~x[1], ~x[0], CLK);  // AND_Gate
  Register #(.width(32), .trigger("high")) x1 (.D(y_star), .Q(x1_output), .clk(and_19_out), .clr(Reset));  // open: en
  and and_19 (and_19_out, ~x[4], ~x[3], ~x[2], ~x[1], x[0], CLK);  // AND_Gate
  Register #(.width(32), .trigger("high")) x2 (.D(y_star), .Q(x2_output), .clk(and_20_out), .clr(Reset));  // open: en
  and and_20 (and_20_out, ~x[4], ~x[3], ~x[2], x[1], ~x[0], CLK);  // AND_Gate
  Register #(.width(32), .trigger("high")) x3 (.D(y_star), .Q(x3_output), .clk(and_21_out), .clr(Reset));  // open: en
  and and_21 (and_21_out, ~x[4], ~x[3], ~x[2], x[1], x[0], CLK);  // AND_Gate
  Register #(.width(32), .trigger("high")) x4 (.D(y_star), .Q(x4_output), .clk(and_22_out), .clr(Reset));  // open: en
  and and_22 (and_22_out, ~x[4], ~x[3], x[2], ~x[1], ~x[0], CLK);  // AND_Gate
  Register #(.width(32), .trigger("high")) x5 (.D(y_star), .Q(x5_output), .clk(and_23_out), .clr(Reset));  // open: en
  and and_23 (and_23_out, ~x[4], ~x[3], x[2], ~x[1], x[0], CLK);  // AND_Gate
  Register #(.width(32), .trigger("high")) x6 (.D(y_star), .Q(x6_output), .clk(and_24_out), .clr(Reset));  // open: en
  and and_24 (and_24_out, ~x[4], ~x[3], x[2], x[1], ~x[0], CLK);  // AND_Gate
  Register #(.width(32), .trigger("high")) x7 (.D(y_star), .Q(x7_output), .clk(and_25_out), .clr(Reset));  // open: en
  and and_25 (and_25_out, ~x[4], ~x[3], x[2], x[1], x[0], CLK);  // AND_Gate
  Register #(.width(32), .trigger("high")) x8 (.D(y_star), .Q(x8_output), .clk(and_26_out), .clr(Reset));  // open: en
  and and_26 (and_26_out, ~x[4], x[3], ~x[2], ~x[1], ~x[0], CLK);  // AND_Gate
  Register #(.width(32), .trigger("high")) x9 (.D(y_star), .Q(x9_output), .clk(and_27_out), .clr(Reset));  // open: en
  and and_27 (and_27_out, ~x[4], x[3], ~x[2], ~x[1], x[0], CLK);  // AND_Gate
  Register #(.width(32), .trigger("high")) x10 (.D(y_star), .Q(x10_output), .clk(and_28_out), .clr(Reset));  // open: en
  and and_28 (and_28_out, ~x[4], x[3], ~x[2], x[1], ~x[0], CLK);  // AND_Gate
  Register #(.width(32), .trigger("high")) x11 (.D(y_star), .Q(x11_output), .clk(and_29_out), .clr(Reset));  // open: en
  and and_29 (and_29_out, ~x[4], x[3], ~x[2], x[1], x[0], CLK);  // AND_Gate
  Register #(.width(32), .trigger("high")) x12 (.D(y_star), .Q(x12_output), .clk(and_30_out), .clr(Reset));  // open: en
  and and_30 (and_30_out, ~x[4], x[3], x[2], ~x[1], ~x[0], CLK);  // AND_Gate
  Register #(.width(32), .trigger("high")) x13 (.D(y_star), .Q(x13_output), .clk(and_31_out), .clr(Reset));  // open: en
  and and_31 (and_31_out, ~x[4], x[3], x[2], ~x[1], x[0], CLK);  // AND_Gate
  Register #(.width(32), .trigger("high")) x14 (.D(y_star), .Q(x14_output), .clk(and_32_out), .clr(Reset));  // open: en
  and and_32 (and_32_out, ~x[4], x[3], x[2], x[1], ~x[0], CLK);  // AND_Gate
  Register #(.width(32), .trigger("high")) x15 (.D(y_star), .Q(x15_output), .clk(and_33_out), .clr(Reset));  // open: en
  and and_33 (and_33_out, ~x[4], x[3], x[2], x[1], x[0], CLK);  // AND_Gate
endmodule

module draw_memory (
  input  save,
  input  reset,
  input  [31:0] in_3,
  input  [31:0] in_4,
  input  [31:0] in_5,
  input  [31:0] in_6,
  input  [31:0] in_7,
  input  [31:0] in_8,
  input  [31:0] in_9,
  input  [31:0] in_10,
  input  [31:0] in_11,
  input  [31:0] in_12,
  input  [31:0] in_13,
  input  [31:0] in_14,
  input  [31:0] in_15,
  input  [31:0] in_16,
  input  [31:0] in_17,
  input  [31:0] in_18,
  input  [31:0] in_19,
  input  [31:0] in_20,
  input  [31:0] in_21,
  input  [31:0] in_22,
  input  [31:0] in_23,
  input  [31:0] in_24,
  input  [31:0] in_25,
  input  [31:0] in_26,
  input  [31:0] in_27,
  input  [31:0] in_28,
  input  [31:0] in_29,
  input  [31:0] in_30,
  input  [31:0] in_31,
  input  [31:0] in_32,
  input  [31:0] in_33,
  input  [31:0] in_34,
  output [31:0] out_35,
  output [31:0] out_36,
  output [31:0] out_37,
  output [31:0] out_38,
  output [31:0] out_39,
  output [31:0] out_40,
  output [31:0] out_41,
  output [31:0] out_42,
  output [31:0] out_43,
  output [31:0] out_44,
  output [31:0] out_45,
  output [31:0] out_46,
  output [31:0] out_47,
  output [31:0] out_48,
  output [31:0] out_49,
  output [31:0] out_50,
  output [31:0] out_51,
  output [31:0] out_52,
  output [31:0] out_53,
  output [31:0] out_54,
  output [31:0] out_55,
  output [31:0] out_56,
  output [31:0] out_57,
  output [31:0] out_58,
  output [31:0] out_59,
  output [31:0] out_60,
  output [31:0] out_61,
  output [31:0] out_62,
  output [31:0] out_63,
  output [31:0] out_64,
  output [31:0] out_65,
  output [31:0] out_66
);

  Register #(.width(32)) register_1 (.D(in_3), .Q(out_35), .clk(save), .clr(reset));  // open: en
  Register #(.width(32)) register_2 (.D(in_4), .Q(out_36), .clk(save), .clr(reset));  // open: en
  Register #(.width(32)) register_3 (.D(in_5), .Q(out_37), .clk(save), .clr(reset));  // open: en
  Register #(.width(32)) register_4 (.D(in_6), .Q(out_38), .clk(save), .clr(reset));  // open: en
  Register #(.width(32)) register_5 (.D(in_7), .Q(out_39), .clk(save), .clr(reset));  // open: en
  Register #(.width(32)) register_6 (.D(in_8), .Q(out_40), .clk(save), .clr(reset));  // open: en
  Register #(.width(32)) register_7 (.D(in_9), .Q(out_41), .clk(save), .clr(reset));  // open: en
  Register #(.width(32)) register_8 (.D(in_10), .Q(out_42), .clk(save), .clr(reset));  // open: en
  Register #(.width(32)) register_9 (.D(in_11), .Q(out_43), .clk(save), .clr(reset));  // open: en
  Register #(.width(32)) register_10 (.D(in_12), .Q(out_44), .clk(save), .clr(reset));  // open: en
  Register #(.width(32)) register_11 (.D(in_13), .Q(out_45), .clk(save), .clr(reset));  // open: en
  Register #(.width(32)) register_12 (.D(in_14), .Q(out_46), .clk(save), .clr(reset));  // open: en
  Register #(.width(32)) register_13 (.D(in_15), .Q(out_47), .clk(save), .clr(reset));  // open: en
  Register #(.width(32)) register_14 (.D(in_16), .Q(out_48), .clk(save), .clr(reset));  // open: en
  Register #(.width(32)) register_15 (.D(in_17), .Q(out_49), .clk(save), .clr(reset));  // open: en
  Register #(.width(32)) register_16 (.D(in_18), .Q(out_50), .clk(save), .clr(reset));  // open: en
  Register #(.width(32)) register_17 (.D(in_19), .Q(out_51), .clk(save), .clr(reset));  // open: en
  Register #(.width(32)) register_18 (.D(in_20), .Q(out_52), .clk(save), .clr(reset));  // open: en
  Register #(.width(32)) register_19 (.D(in_21), .Q(out_53), .clk(save), .clr(reset));  // open: en
  Register #(.width(32)) register_20 (.D(in_22), .Q(out_54), .clk(save), .clr(reset));  // open: en
  Register #(.width(32)) register_21 (.D(in_23), .Q(out_55), .clk(save), .clr(reset));  // open: en
  Register #(.width(32)) register_22 (.D(in_24), .Q(out_56), .clk(save), .clr(reset));  // open: en
  Register #(.width(32)) register_23 (.D(in_25), .Q(out_57), .clk(save), .clr(reset));  // open: en
  Register #(.width(32)) register_24 (.D(in_26), .Q(out_58), .clk(save), .clr(reset));  // open: en
  Register #(.width(32)) register_25 (.D(in_27), .Q(out_59), .clk(save), .clr(reset));  // open: en
  Register #(.width(32)) register_26 (.D(in_28), .Q(out_60), .clk(save), .clr(reset));  // open: en
  Register #(.width(32)) register_27 (.D(in_29), .Q(out_61), .clk(save), .clr(reset));  // open: en
  Register #(.width(32)) register_28 (.D(in_30), .Q(out_62), .clk(save), .clr(reset));  // open: en
  Register #(.width(32)) register_29 (.D(in_31), .Q(out_63), .clk(save), .clr(reset));  // open: en
  Register #(.width(32)) register_30 (.D(in_32), .Q(out_64), .clk(save), .clr(reset));  // open: en
  Register #(.width(32)) register_31 (.D(in_33), .Q(out_65), .clk(save), .clr(reset));  // open: en
  Register #(.width(32)) register_32 (.D(in_34), .Q(out_66), .clk(save), .clr(reset));  // open: en
endmodule

module drawer (
  input  [1:0] in_1,
  input  [31:0] y0_saved,
  input  [31:0] y0,
  input  [31:0] in_4,
  input  [31:0] in_5,
  input  [31:0] in_6,
  input  [31:0] in_7,
  input  [31:0] in_8,
  input  [31:0] in_9,
  input  [31:0] in_10,
  input  [31:0] in_11,
  input  [31:0] in_12,
  input  [31:0] in_13,
  input  [31:0] in_14,
  input  [31:0] in_15,
  input  [31:0] in_16,
  input  [31:0] in_17,
  input  [31:0] in_18,
  input  [31:0] in_19,
  input  [31:0] in_20,
  input  [31:0] in_21,
  input  [31:0] in_22,
  input  [31:0] in_23,
  input  [31:0] in_24,
  input  [31:0] in_25,
  input  [31:0] in_26,
  input  [31:0] in_27,
  input  [31:0] in_28,
  input  [31:0] in_29,
  input  [31:0] in_30,
  input  [31:0] in_31,
  input  [31:0] in_32,
  input  [31:0] in_33,
  input  [31:0] in_34,
  input  [31:0] in_35,
  input  [31:0] in_36,
  input  [31:0] in_37,
  input  [31:0] in_38,
  input  [31:0] in_39,
  input  [31:0] in_40,
  input  [31:0] in_41,
  input  [31:0] in_42,
  input  [31:0] in_43,
  input  [31:0] in_44,
  input  [31:0] in_45,
  input  [31:0] in_46,
  input  [31:0] in_47,
  input  [31:0] in_48,
  input  [31:0] in_49,
  input  [31:0] in_50,
  input  [31:0] in_51,
  input  [31:0] in_52,
  input  [31:0] in_53,
  input  [31:0] in_54,
  input  [31:0] in_55,
  input  [31:0] in_56,
  input  [31:0] in_57,
  input  [31:0] in_58,
  input  [31:0] in_59,
  input  [31:0] in_60,
  input  [31:0] in_61,
  input  [31:0] in_62,
  input  [31:0] in_63,
  input  [31:0] in_64,
  input  [31:0] in_65,
  output [31:0] y0_merged,
  output [31:0] out_67,
  output [31:0] out_68,
  output [31:0] out_69,
  output [31:0] out_70,
  output [31:0] out_71,
  output [31:0] out_72,
  output [31:0] out_73,
  output [31:0] out_74,
  output [31:0] out_75,
  output [31:0] out_76,
  output [31:0] out_77,
  output [31:0] out_78,
  output [31:0] out_79,
  output [31:0] out_80,
  output [31:0] out_81,
  output [31:0] out_82,
  output [31:0] out_83,
  output [31:0] out_84,
  output [31:0] out_85,
  output [31:0] out_86,
  output [31:0] out_87,
  output [31:0] out_88,
  output [31:0] out_89,
  output [31:0] out_90,
  output [31:0] out_91,
  output [31:0] out_92,
  output [31:0] out_93,
  output [31:0] out_94,
  output [31:0] out_95,
  output [31:0] out_96,
  output [31:0] out_97
);

  wire [31:0] draw_operator_1_added, draw_operator_1_merged, draw_operator_1_substracted,
       draw_operator_2_added, draw_operator_2_merged, draw_operator_2_substracted, draw_operator_3_added,
       draw_operator_3_merged, draw_operator_3_substracted, draw_operator_4_added, draw_operator_4_merged,
       draw_operator_4_substracted, draw_operator_5_added, draw_operator_5_merged,
       draw_operator_5_substracted, draw_operator_6_added, draw_operator_6_merged,
       draw_operator_6_substracted, draw_operator_7_added, draw_operator_7_merged,
       draw_operator_7_substracted, draw_operator_8_added, draw_operator_8_merged,
       draw_operator_8_substracted, draw_operator_9_added, draw_operator_9_merged,
       draw_operator_9_substracted, draw_operator_10_added, draw_operator_10_merged,
       draw_operator_10_substracted, draw_operator_11_added, draw_operator_11_merged,
       draw_operator_11_substracted, draw_operator_12_added, draw_operator_12_merged,
       draw_operator_12_substracted, draw_operator_13_added, draw_operator_13_merged,
       draw_operator_13_substracted, draw_operator_14_added, draw_operator_14_merged,
       draw_operator_14_substracted, draw_operator_15_added, draw_operator_15_merged,
       draw_operator_15_substracted, draw_operator_16_added, draw_operator_16_merged,
       draw_operator_16_substracted, draw_operator_17_added, draw_operator_17_merged,
       draw_operator_17_substracted, draw_operator_18_added, draw_operator_18_merged,
       draw_operator_18_substracted, draw_operator_19_added, draw_operator_19_merged,
       draw_operator_19_substracted, draw_operator_20_added, draw_operator_20_merged,
       draw_operator_20_substracted, draw_operator_21_added, draw_operator_21_merged,
       draw_operator_21_substracted, draw_operator_22_added, draw_operator_22_merged,
       draw_operator_22_substracted, draw_operator_23_added, draw_operator_23_merged,
       draw_operator_23_substracted, draw_operator_24_added, draw_operator_24_merged,
       draw_operator_24_substracted, draw_operator_25_added, draw_operator_25_merged,
       draw_operator_25_substracted, draw_operator_26_added, draw_operator_26_merged,
       draw_operator_26_substracted, draw_operator_27_added, draw_operator_27_merged,
       draw_operator_27_substracted, draw_operator_28_added, draw_operator_28_merged,
       draw_operator_28_substracted, draw_operator_29_added, draw_operator_29_merged,
       draw_operator_29_substracted, draw_operator_30_added, draw_operator_30_merged,
       draw_operator_30_substracted, draw_operator_31_added, draw_operator_31_merged,
       draw_operator_31_substracted, draw_operator_32_added, draw_operator_32_merged,
       draw_operator_32_substracted;

  draw_operator draw_operator_1 (
    .A1(y0_saved), .A2(y0), .added(draw_operator_1_added), .merged(draw_operator_1_merged),
    .substracted(draw_operator_1_substracted));
  draw_operator draw_operator_2 (
    .A1(in_4), .A2(in_5), .added(draw_operator_2_added), .merged(draw_operator_2_merged),
    .substracted(draw_operator_2_substracted));
  draw_operator draw_operator_3 (
    .A1(in_6), .A2(in_7), .added(draw_operator_3_added), .merged(draw_operator_3_merged),
    .substracted(draw_operator_3_substracted));
  draw_operator draw_operator_4 (
    .A1(in_8), .A2(in_9), .added(draw_operator_4_added), .merged(draw_operator_4_merged),
    .substracted(draw_operator_4_substracted));
  draw_operator draw_operator_5 (
    .A1(in_10), .A2(in_11), .added(draw_operator_5_added), .merged(draw_operator_5_merged),
    .substracted(draw_operator_5_substracted));
  draw_operator draw_operator_6 (
    .A1(in_12), .A2(in_13), .added(draw_operator_6_added), .merged(draw_operator_6_merged),
    .substracted(draw_operator_6_substracted));
  draw_operator draw_operator_7 (
    .A1(in_14), .A2(in_15), .added(draw_operator_7_added), .merged(draw_operator_7_merged),
    .substracted(draw_operator_7_substracted));
  draw_operator draw_operator_8 (
    .A1(in_16), .A2(in_17), .added(draw_operator_8_added), .merged(draw_operator_8_merged),
    .substracted(draw_operator_8_substracted));
  draw_operator draw_operator_9 (
    .A1(in_18), .A2(in_19), .added(draw_operator_9_added), .merged(draw_operator_9_merged),
    .substracted(draw_operator_9_substracted));
  draw_operator draw_operator_10 (
    .A1(in_20), .A2(in_21), .added(draw_operator_10_added), .merged(draw_operator_10_merged),
    .substracted(draw_operator_10_substracted));
  draw_operator draw_operator_11 (
    .A1(in_22), .A2(in_23), .added(draw_operator_11_added), .merged(draw_operator_11_merged),
    .substracted(draw_operator_11_substracted));
  draw_operator draw_operator_12 (
    .A1(in_24), .A2(in_25), .added(draw_operator_12_added), .merged(draw_operator_12_merged),
    .substracted(draw_operator_12_substracted));
  draw_operator draw_operator_13 (
    .A1(in_26), .A2(in_27), .added(draw_operator_13_added), .merged(draw_operator_13_merged),
    .substracted(draw_operator_13_substracted));
  draw_operator draw_operator_14 (
    .A1(in_28), .A2(in_29), .added(draw_operator_14_added), .merged(draw_operator_14_merged),
    .substracted(draw_operator_14_substracted));
  draw_operator draw_operator_15 (
    .A1(in_30), .A2(in_31), .added(draw_operator_15_added), .merged(draw_operator_15_merged),
    .substracted(draw_operator_15_substracted));
  draw_operator draw_operator_16 (
    .A1(in_32), .A2(in_33), .added(draw_operator_16_added), .merged(draw_operator_16_merged),
    .substracted(draw_operator_16_substracted));
  draw_operator draw_operator_17 (
    .A1(in_34), .A2(in_35), .added(draw_operator_17_added), .merged(draw_operator_17_merged),
    .substracted(draw_operator_17_substracted));
  draw_operator draw_operator_18 (
    .A1(in_36), .A2(in_37), .added(draw_operator_18_added), .merged(draw_operator_18_merged),
    .substracted(draw_operator_18_substracted));
  draw_operator draw_operator_19 (
    .A1(in_38), .A2(in_39), .added(draw_operator_19_added), .merged(draw_operator_19_merged),
    .substracted(draw_operator_19_substracted));
  draw_operator draw_operator_20 (
    .A1(in_40), .A2(in_41), .added(draw_operator_20_added), .merged(draw_operator_20_merged),
    .substracted(draw_operator_20_substracted));
  draw_operator draw_operator_21 (
    .A1(in_42), .A2(in_43), .added(draw_operator_21_added), .merged(draw_operator_21_merged),
    .substracted(draw_operator_21_substracted));
  draw_operator draw_operator_22 (
    .A1(in_44), .A2(in_45), .added(draw_operator_22_added), .merged(draw_operator_22_merged),
    .substracted(draw_operator_22_substracted));
  draw_operator draw_operator_23 (
    .A1(in_46), .A2(in_47), .added(draw_operator_23_added), .merged(draw_operator_23_merged),
    .substracted(draw_operator_23_substracted));
  draw_operator draw_operator_24 (
    .A1(in_48), .A2(in_49), .added(draw_operator_24_added), .merged(draw_operator_24_merged),
    .substracted(draw_operator_24_substracted));
  draw_operator draw_operator_25 (
    .A1(in_50), .A2(in_51), .added(draw_operator_25_added), .merged(draw_operator_25_merged),
    .substracted(draw_operator_25_substracted));
  draw_operator draw_operator_26 (
    .A1(in_52), .A2(in_53), .added(draw_operator_26_added), .merged(draw_operator_26_merged),
    .substracted(draw_operator_26_substracted));
  draw_operator draw_operator_27 (
    .A1(in_54), .A2(in_55), .added(draw_operator_27_added), .merged(draw_operator_27_merged),
    .substracted(draw_operator_27_substracted));
  draw_operator draw_operator_28 (
    .A1(in_56), .A2(in_57), .added(draw_operator_28_added), .merged(draw_operator_28_merged),
    .substracted(draw_operator_28_substracted));
  draw_operator draw_operator_29 (
    .A1(in_58), .A2(in_59), .added(draw_operator_29_added), .merged(draw_operator_29_merged),
    .substracted(draw_operator_29_substracted));
  draw_operator draw_operator_30 (
    .A1(in_60), .A2(in_61), .added(draw_operator_30_added), .merged(draw_operator_30_merged),
    .substracted(draw_operator_30_substracted));
  draw_operator draw_operator_31 (
    .A1(in_62), .A2(in_63), .added(draw_operator_31_added), .merged(draw_operator_31_merged),
    .substracted(draw_operator_31_substracted));
  draw_operator draw_operator_32 (
    .A1(in_64), .A2(in_65), .added(draw_operator_32_added), .merged(draw_operator_32_merged),
    .substracted(draw_operator_32_substracted));
  Multiplexer #(.select(2), .width(32)) multiplexer_1 (
    .in0(draw_operator_1_merged), .in1(draw_operator_1_added), .in2(draw_operator_1_substracted),
    .out(y0_merged), .sel(in_1));  // open: in3, en
  Multiplexer #(.select(2), .width(32)) multiplexer_2 (
    .in0(draw_operator_2_merged), .in1(draw_operator_2_added), .in2(draw_operator_2_substracted),
    .out(out_67), .sel(in_1));  // open: in3, en
  Multiplexer #(.select(2), .width(32)) multiplexer_3 (
    .in0(draw_operator_3_merged), .in1(draw_operator_3_added), .in2(draw_operator_3_substracted),
    .out(out_68), .sel(in_1));  // open: in3, en
  Multiplexer #(.select(2), .width(32)) multiplexer_4 (
    .in0(draw_operator_4_merged), .in1(draw_operator_4_added), .in2(draw_operator_4_substracted),
    .out(out_69), .sel(in_1));  // open: in3, en
  Multiplexer #(.select(2), .width(32)) multiplexer_5 (
    .in0(draw_operator_5_merged), .in1(draw_operator_5_added), .in2(draw_operator_5_substracted),
    .out(out_70), .sel(in_1));  // open: in3, en
  Multiplexer #(.select(2), .width(32)) multiplexer_6 (
    .in0(draw_operator_6_merged), .in1(draw_operator_6_added), .in2(draw_operator_6_substracted),
    .out(out_71), .sel(in_1));  // open: in3, en
  Multiplexer #(.select(2), .width(32)) multiplexer_7 (
    .in0(draw_operator_7_merged), .in1(draw_operator_7_added), .in2(draw_operator_7_substracted),
    .out(out_72), .sel(in_1));  // open: in3, en
  Multiplexer #(.select(2), .width(32)) multiplexer_8 (
    .in0(draw_operator_8_merged), .in1(draw_operator_8_added), .in2(draw_operator_8_substracted),
    .out(out_73), .sel(in_1));  // open: in3, en
  Multiplexer #(.select(2), .width(32)) multiplexer_9 (
    .in0(draw_operator_9_merged), .in1(draw_operator_9_added), .in2(draw_operator_9_substracted),
    .out(out_74), .sel(in_1));  // open: in3, en
  Multiplexer #(.select(2), .width(32)) multiplexer_10 (
    .in0(draw_operator_10_merged), .in1(draw_operator_10_added), .in2(draw_operator_10_substracted),
    .out(out_75), .sel(in_1));  // open: in3, en
  Multiplexer #(.select(2), .width(32)) multiplexer_11 (
    .in0(draw_operator_11_merged), .in1(draw_operator_11_added), .in2(draw_operator_11_substracted),
    .out(out_76), .sel(in_1));  // open: in3, en
  Multiplexer #(.select(2), .width(32)) multiplexer_12 (
    .in0(draw_operator_12_merged), .in1(draw_operator_12_added), .in2(draw_operator_12_substracted),
    .out(out_77), .sel(in_1));  // open: in3, en
  Multiplexer #(.select(2), .width(32)) multiplexer_13 (
    .in0(draw_operator_13_merged), .in1(draw_operator_13_added), .in2(draw_operator_13_substracted),
    .out(out_78), .sel(in_1));  // open: in3, en
  Multiplexer #(.select(2), .width(32)) multiplexer_14 (
    .in0(draw_operator_14_merged), .in1(draw_operator_14_added), .in2(draw_operator_14_substracted),
    .out(out_79), .sel(in_1));  // open: in3, en
  Multiplexer #(.select(2), .width(32)) multiplexer_15 (
    .in0(draw_operator_15_merged), .in1(draw_operator_15_added), .in2(draw_operator_15_substracted),
    .out(out_80), .sel(in_1));  // open: in3, en
  Multiplexer #(.select(2), .width(32)) multiplexer_16 (
    .in0(draw_operator_16_merged), .in1(draw_operator_16_added), .in2(draw_operator_16_substracted),
    .out(out_81), .sel(in_1));  // open: in3, en
  Multiplexer #(.select(2), .width(32)) multiplexer_17 (
    .in0(draw_operator_17_merged), .in1(draw_operator_17_added), .in2(draw_operator_17_substracted),
    .out(out_82), .sel(in_1));  // open: in3, en
  Multiplexer #(.select(2), .width(32)) multiplexer_18 (
    .in0(draw_operator_18_merged), .in1(draw_operator_18_added), .in2(draw_operator_18_substracted),
    .out(out_83), .sel(in_1));  // open: in3, en
  Multiplexer #(.select(2), .width(32)) multiplexer_19 (
    .in0(draw_operator_19_merged), .in1(draw_operator_19_added), .in2(draw_operator_19_substracted),
    .out(out_84), .sel(in_1));  // open: in3, en
  Multiplexer #(.select(2), .width(32)) multiplexer_20 (
    .in0(draw_operator_20_merged), .in1(draw_operator_20_added), .in2(draw_operator_20_substracted),
    .out(out_85), .sel(in_1));  // open: in3, en
  Multiplexer #(.select(2), .width(32)) multiplexer_21 (
    .in0(draw_operator_21_merged), .in1(draw_operator_21_added), .in2(draw_operator_21_substracted),
    .out(out_86), .sel(in_1));  // open: in3, en
  Multiplexer #(.select(2), .width(32)) multiplexer_22 (
    .in0(draw_operator_22_merged), .in1(draw_operator_22_added), .in2(draw_operator_22_substracted),
    .out(out_87), .sel(in_1));  // open: in3, en
  Multiplexer #(.select(2), .width(32)) multiplexer_23 (
    .in0(draw_operator_23_merged), .in1(draw_operator_23_added), .in2(draw_operator_23_substracted),
    .out(out_88), .sel(in_1));  // open: in3, en
  Multiplexer #(.select(2), .width(32)) multiplexer_24 (
    .in0(draw_operator_24_merged), .in1(draw_operator_24_added), .in2(draw_operator_24_substracted),
    .out(out_89), .sel(in_1));  // open: in3, en
  Multiplexer #(.select(2), .width(32)) multiplexer_25 (
    .in0(draw_operator_25_merged), .in1(draw_operator_25_added), .in2(draw_operator_25_substracted),
    .out(out_90), .sel(in_1));  // open: in3, en
  Multiplexer #(.select(2), .width(32)) multiplexer_26 (
    .in0(draw_operator_26_merged), .in1(draw_operator_26_added), .in2(draw_operator_26_substracted),
    .out(out_91), .sel(in_1));  // open: in3, en
  Multiplexer #(.select(2), .width(32)) multiplexer_27 (
    .in0(draw_operator_27_merged), .in1(draw_operator_27_added), .in2(draw_operator_27_substracted),
    .out(out_92), .sel(in_1));  // open: in3, en
  Multiplexer #(.select(2), .width(32)) multiplexer_28 (
    .in0(draw_operator_28_merged), .in1(draw_operator_28_added), .in2(draw_operator_28_substracted),
    .out(out_93), .sel(in_1));  // open: in3, en
  Multiplexer #(.select(2), .width(32)) multiplexer_29 (
    .in0(draw_operator_29_merged), .in1(draw_operator_29_added), .in2(draw_operator_29_substracted),
    .out(out_94), .sel(in_1));  // open: in3, en
  Multiplexer #(.select(2), .width(32)) multiplexer_30 (
    .in0(draw_operator_30_merged), .in1(draw_operator_30_added), .in2(draw_operator_30_substracted),
    .out(out_95), .sel(in_1));  // open: in3, en
  Multiplexer #(.select(2), .width(32)) multiplexer_31 (
    .in0(draw_operator_31_merged), .in1(draw_operator_31_added), .in2(draw_operator_31_substracted),
    .out(out_96), .sel(in_1));  // open: in3, en
  Multiplexer #(.select(2), .width(32)) multiplexer_32 (
    .in0(draw_operator_32_merged), .in1(draw_operator_32_added), .in2(draw_operator_32_substracted),
    .out(out_97), .sel(in_1));  // open: in3, en

  // Other names for the same wires on the sheet: op_code[1:0] = in_1
endmodule

module back_memory (
  input  [3:0] x_2,
  input  [3:0] x,
  input  [3:0] q,
  input  completo,
  input  back,
  input  ok,
  input  [1:0] select,
  input  reset,
  output [3:0] out_9,
  output [3:0] out_10,
  output [3:0] out_11,
  output [1:0] out_12
);

  wire or_1_out, or_3_out;
  wire [1:0] or_2_out;

  or or_1 (or_1_out, completo, back, ok);
  assign or_2_out = {2{completo}} | select;  // OR_Gate or_2, 2 bits wide
  Register #(.width(2)) register_1 (.D(or_2_out), .Q(out_12), .clk(or_3_out), .clr(reset));  // open: en
  or or_3 (or_3_out, completo, ok);
  Register #(.width(4)) register_2 (.D(x_2), .Q(out_9), .clk(or_1_out), .clr(reset));  // open: en
  Register #(.width(4)) register_3 (.D(x), .Q(out_10), .clk(or_1_out), .clr(reset));  // open: en
  Register #(.width(4)) register_4 (.D(q), .Q(out_11), .clk(or_1_out), .clr(reset));  // open: en
endmodule

module draw_operator (
  input  [31:0] A1,
  input  [31:0] A2,
  output [31:0] added,
  output [31:0] merged,
  output [31:0] substracted
);

  wire a_of, and_2_out, floating, or_3_out, or_4_out, or_5_out, priority_encoder_1_p2, priority_encoder_1_p3,
       s_of;
  wire [4:0] adder_1_out, priority_encoder_1_p4, priority_encoder_2_out, subtractor_1_out;
  wire [31:0] complete_decoder_1_out_2, complete_decoder_2_out_2, multiplexer_1_out, zero_zero;

  or or_1 (floating, priority_encoder_1_p2, priority_encoder_1_p3);
  assign zero_zero = A2 & A1;  // AND_Gate and_1, 32 bits wide
  assign merged = A1 | A2;  // OR_Gate or_2, 32 bits wide
  // Priority_Encoder #(.select(5)) priority_encoder_1: pin names not known; wires that end beside it: A2, priority_encoder_1_p2, priority_encoder_1_p3, priority_encoder_1_p4
  Adder #(.width(5)) adder_1 (
    .a(priority_encoder_1_p4), .b(priority_encoder_2_out), .out(adder_1_out), .cout(a_of));  // open: cin
  Subtractor #(.width(5)) subtractor_1 (
    .a(priority_encoder_1_p4), .b(priority_encoder_2_out), .out(subtractor_1_out), .bout(s_of));  // open: bin
  Priority_Encoder #(.select(5)) priority_encoder_2 (
    .in0(A2[0]), .in1(A2[1]), .in2(A2[2]), .in3(A2[3]), .in4(A2[4]), .in5(A2[5]), .in6(A2[6]), .in7(A2[7]),
    .in8(A2[8]), .in9(A2[9]), .in10(A2[10]), .in11(A2[11]), .in12(A2[12]), .in13(A2[13]), .in14(A2[14]),
    .in15(A2[15]), .in16(A2[16]), .in17(A2[17]), .in18(A2[18]), .in19(A2[19]), .in20(A2[20]), .in21(A2[21]),
    .in22(A2[22]), .in23(A2[23]), .in24(A2[24]), .in25(A2[25]), .in26(A2[26]), .in27(A2[27]), .in28(A2[28]),
    .in29(A2[29]), .in30(A2[30]), .in31(A2[31]), .out(priority_encoder_2_out));
  complete_decoder complete_decoder_1 (.y(adder_1_out), .out_2(complete_decoder_1_out_2));
  complete_decoder complete_decoder_2 (.y(subtractor_1_out), .out_2(complete_decoder_2_out_2));
  Multiplexer #(.width(32)) multiplexer_1 (
    .in0({32{1'b0}}), .in1(32'h1), .out(multiplexer_1_out), .sel(and_2_out));  // open: en
  and and_2 (and_2_out, zero_zero[0], ~zero_zero[1], ~zero_zero[2], ~zero_zero[3], ~zero_zero[4], ~zero_zero[5], ~zero_zero[6], ~zero_zero[7], ~zero_zero[8], ~zero_zero[9], ~zero_zero[10], ~zero_zero[11], ~zero_zero[12], ~zero_zero[13], ~zero_zero[14], ~zero_zero[15], ~zero_zero[17], ~zero_zero[18], ~zero_zero[19], ~zero_zero[20], ~zero_zero[21], ~zero_zero[22], ~zero_zero[23], ~zero_zero[24], ~zero_zero[25], ~zero_zero[26], ~zero_zero[27], ~zero_zero[28], ~zero_zero[29], ~zero_zero[30], ~zero_zero[31], ~zero_zero[16]);  // AND_Gate
  Multiplexer #(.width(32)) multiplexer_2 (
    .in0(complete_decoder_1_out_2), .in1({32{1'b0}}), .out(added), .sel(or_3_out));  // open: en
  or or_3 (or_3_out, floating, a_of);
  Multiplexer #(.width(32)) multiplexer_3 (
    .in0(complete_decoder_2_out_2), .in1(multiplexer_1_out), .out(substracted), .sel(or_4_out));  // open: en
  or or_4 (or_4_out, floating, or_5_out);
  or or_5 (or_5_out, and_2_out, s_of);
endmodule

module complete_decoder (
  input  [4:0] y,
  output [31:0] out_2
);

  Decoder #(.select(5)) decoder_1 (
    .out0(out_2[0]), .out1(out_2[1]), .out2(out_2[2]), .out3(out_2[3]), .out4(out_2[4]), .out5(out_2[5]),
    .out6(out_2[6]), .out7(out_2[7]), .out8(out_2[8]), .out9(out_2[9]), .out10(out_2[10]), .out11(out_2[11]),
    .out12(out_2[12]), .out13(out_2[13]), .out14(out_2[14]), .out15(out_2[15]), .out16(out_2[16]),
    .out17(out_2[17]), .out18(out_2[18]), .out19(out_2[19]), .out20(out_2[20]), .out21(out_2[21]),
    .out22(out_2[22]), .out23(out_2[23]), .out24(out_2[24]), .out25(out_2[25]), .out26(out_2[26]),
    .out27(out_2[27]), .out28(out_2[28]), .out29(out_2[29]), .out30(out_2[30]), .out31(out_2[31]), .sel(y));  // open: en
endmodule

module saved_memory (
  input  [3:0] x_2,
  input  [3:0] x,
  input  [3:0] q,
  input  save,
  input  reset,
  output [3:0] out_6,
  output [3:0] out_7,
  output [3:0] out_8
);

  Register #(.width(4)) register_1 (.D(x_2), .Q(out_6), .clk(save), .clr(reset));  // open: en
  Register #(.width(4)) register_2 (.D(x), .Q(out_7), .clk(save), .clr(reset));  // open: en
  Register #(.width(4)) register_3 (.D(q), .Q(out_8), .clk(save), .clr(reset));  // open: en
endmodule

module m_ui (
  input  _9,
  input  _8,
  input  _7,
  input  _6,
  input  _5,
  input  _4,
  input  _3,
  input  _2,
  input  _1,
  input  _0,
  input  reset,
  input  azzera,
  input  back,
  input  ok,
  input  right,
  input  left,
  input  save,
  input  load,
  input  cancella,
  input  op,
  output [3:0] data,
  output click,
  output reset_2,
  output azzera_2,
  output back_2,
  output ok_2,
  output right_2,
  output left_2,
  output save_2,
  output load_2,
  output cancella_2,
  output [1:0] select,
  output [1:0] op_code
);

  wire not_1_out, not_2_out, or_1_out, or_2_out;

  or or_1 (or_1_out, ok, right, left);
  Counter #(.width(2), .max('h2), .trigger("falling")) counter_1 (
    .Q(op_code), .clk(op), .clr(reset));  // open: load, D, count, carry
  not not_1 (not_1_out, not_2_out);
  Counter #(.width(2), .max('h2), .ongoal("stay"), .trigger("falling")) counter_2 (
    .load(not_1_out), .count(not_2_out), .Q(select), .clk(or_1_out), .clr(or_2_out));  // open: D, carry
  not not_2 (not_2_out, left);
  or or_2 (or_2_out, reset, azzera, save);
  keypad keypad_1 (
    ._0(_0), ._1(_1), ._3(_3), ._2(_2), ._5(_5), ._4(_4), ._7(_7), ._6(_6), .b2_2(data[2]), .b1(data[1]),
    .b0(data[0]), ._8(_8), ._9(_9), .b2(data[3]), .clicked(click));

  assign azzera_2 = azzera;
  assign back_2 = back;
  assign cancella_2 = cancella;
  assign left_2 = left;
  assign load_2 = load;
  assign ok_2 = ok;
  assign reset_2 = reset;
  assign right_2 = right;
  assign save_2 = save;
endmodule

module m_input_memory (
  input  [3:0] data,
  input  click,
  input  reset,
  input  azzera,
  input  back,
  input  ok,
  input  save,
  input  load,
  input  cancella,
  input  [1:0] select,
  output [3:0] x_2,
  output [3:0] x,
  output [3:0] q,
  output [3:0] x_2_saved,
  output [3:0] x_saved,
  output [3:0] q_saved
);

  wire or_1_out, or_2_out, or_3_out, or_4_out, or_5_out, or_6_out;
  wire [1:0] back_memory_1_out_12, multiplexer_4_out;
  wire [3:0] back_memory_1_out_9, back_memory_1_out_10, back_memory_1_out_11, multiplexer_1_out,
       multiplexer_2_out, multiplexer_3_out;

  or or_1 (or_1_out, azzera, load, save);
  or or_2 (or_2_out, azzera, save, ok, load);
  back_memory back_memory_1 (
    .q(q), .back(back), .out_11(back_memory_1_out_11), .out_12(back_memory_1_out_12), .select(select),
    .reset(or_3_out), .x(x), .x_2(x_2), .out_10(back_memory_1_out_10), .out_9(back_memory_1_out_9),
    .completo(or_1_out), .ok(or_2_out));
  or or_3 (or_3_out, reset, cancella);
  Multiplexer #(.width(4)) multiplexer_1 (
    .in0(back_memory_1_out_9), .in1(x_2_saved), .out(multiplexer_1_out), .sel(load));  // open: en
  Multiplexer #(.width(4)) multiplexer_2 (
    .in0(back_memory_1_out_10), .in1(x_saved), .out(multiplexer_2_out), .sel(load));  // open: en
  Multiplexer #(.width(4)) multiplexer_3 (
    .in0(back_memory_1_out_11), .in1(q_saved), .out(multiplexer_3_out), .sel(load));  // open: en
  saved_memory saved_memory_1 (
    .x_2(x_2), .x(x), .q(q), .save(save), .out_6(x_2_saved), .out_7(x_saved), .out_8(q_saved),
    .reset(or_4_out));
  or or_4 (or_4_out, cancella, reset);
  Multiplexer #(.width(2)) multiplexer_4 (
    .in0(back_memory_1_out_12), .in1(2'b11), .out(multiplexer_4_out), .sel(load));  // open: en
  or or_5 (or_5_out, back, load);
  memory memory_1 (
    .in_1(data), .in_2(click), .in_3(ok), .in_4(select), .out_11(x_2), .out_12(x), .out_13(q),
    .Reset(or_6_out), .back_x_2(multiplexer_1_out), .back_select(multiplexer_4_out), .back_save(or_5_out),
    .back_x(multiplexer_2_out), .back_q(multiplexer_3_out));
  or or_6 (or_6_out, azzera, reset, save);

  // Notes on the sheet:
  //   BACK_MEMORY
  //   SAVED_MEMORY
  //   MAIN_MEMORY
endmodule

module m_calcolatore (
  input  [3:0] c_x_2,
  input  [3:0] c_x,
  input  [3:0] q,
  input  clock,
  input  reset,
  output [4:0] y,
  output of,
  output [4:0] x
);

  wire [4:0] calcolo_1_out_5;

  Counter #(.width(5), .max('h1f)) u_X (.Q(x), .clk(clock), .clr(reset));  // open: load, D, count, carry
  calcolo calcolo_1 (.c_x_2(c_x_2), .c_x(c_x), .q(q), .out_5(calcolo_1_out_5), .x(x), .out_6(of));
  assign y = calcolo_1_out_5 & ~{5{of}};  // AND_Gate and_1, 5 bits wide
endmodule

module m_drawer (
  input  [4:0] x,
  input  [4:0] y,
  input  of,
  input  clock,
  input  reset,
  input  save,
  input  cancella,
  input  [1:0] op_code,
  output [31:0] out_9,
  output [31:0] out_10,
  output [31:0] out_11,
  output [31:0] out_12,
  output [31:0] out_13,
  output [31:0] out_14,
  output [31:0] out_15,
  output [31:0] out_16,
  output [31:0] out_17,
  output [31:0] out_18,
  output [31:0] out_19,
  output [31:0] out_20,
  output [31:0] out_21,
  output [31:0] out_22,
  output [31:0] out_23,
  output [31:0] out_24,
  output [31:0] out_25,
  output [31:0] out_26,
  output [31:0] out_27,
  output [31:0] out_28,
  output [31:0] out_29,
  output [31:0] out_30,
  output [31:0] out_31,
  output [31:0] out_32,
  output [31:0] out_33,
  output [31:0] out_34,
  output [31:0] out_35,
  output [31:0] out_36,
  output [31:0] out_37,
  output [31:0] out_38,
  output [31:0] out_39,
  output [31:0] out_40
);

  wire or_1_out;
  wire [31:0] draw_memory_1_out_35, draw_memory_1_out_36, draw_memory_1_out_37, draw_memory_1_out_38,
       draw_memory_1_out_39, draw_memory_1_out_40, draw_memory_1_out_41, draw_memory_1_out_42,
       draw_memory_1_out_43, draw_memory_1_out_44, draw_memory_1_out_45, draw_memory_1_out_46,
       draw_memory_1_out_47, draw_memory_1_out_48, draw_memory_1_out_49, draw_memory_1_out_50,
       draw_memory_1_out_51, draw_memory_1_out_52, draw_memory_1_out_53, draw_memory_1_out_54,
       draw_memory_1_out_55, draw_memory_1_out_56, draw_memory_1_out_57, draw_memory_1_out_58,
       draw_memory_1_out_59, draw_memory_1_out_60, draw_memory_1_out_61, draw_memory_1_out_62,
       draw_memory_1_out_63, draw_memory_1_out_64, draw_memory_1_out_65, draw_memory_1_out_66, y0, y1, y2,
       y3, y4, y5, y6, y7, y8, y9, y10, y11, y12, y13, y14, y15, y16, y17, y18, y19, y20, y21, y22, y23, y24,
       y25, y26, y27, y28, y29, y30, y31;

  drawer drawer_1 (
    .y0_saved(draw_memory_1_out_35), .y0(y0), .in_4(draw_memory_1_out_36), .in_5(y1),
    .in_6(draw_memory_1_out_37), .in_7(y2), .in_8(draw_memory_1_out_38), .in_9(y3),
    .in_10(draw_memory_1_out_39), .in_11(y4), .in_12(draw_memory_1_out_40), .in_13(y5),
    .in_14(draw_memory_1_out_41), .in_15(y6), .in_16(draw_memory_1_out_42), .in_17(y7),
    .in_18(draw_memory_1_out_43), .in_19(y8), .in_20(draw_memory_1_out_44), .in_21(y9),
    .in_22(draw_memory_1_out_45), .in_23(y10), .in_24(draw_memory_1_out_46), .in_25(y11),
    .in_26(draw_memory_1_out_47), .in_27(y12), .in_28(draw_memory_1_out_48), .in_29(y13),
    .in_30(draw_memory_1_out_49), .in_31(y14), .in_32(draw_memory_1_out_50), .in_33(y15),
    .in_34(draw_memory_1_out_51), .in_35(y16), .in_36(draw_memory_1_out_52), .in_37(y17),
    .in_38(draw_memory_1_out_53), .in_39(y18), .in_40(draw_memory_1_out_54), .in_41(y19),
    .in_42(draw_memory_1_out_55), .in_43(y20), .in_44(draw_memory_1_out_56), .in_45(y21),
    .in_46(draw_memory_1_out_57), .in_47(y22), .in_48(draw_memory_1_out_58), .in_49(y23),
    .in_50(draw_memory_1_out_59), .in_51(y24), .in_52(draw_memory_1_out_60), .in_53(y25),
    .in_54(draw_memory_1_out_61), .in_55(y26), .in_56(draw_memory_1_out_62), .in_57(y27),
    .in_58(draw_memory_1_out_63), .in_59(y28), .in_60(draw_memory_1_out_64), .in_61(y29),
    .in_62(draw_memory_1_out_65), .in_63(y30), .in_64(draw_memory_1_out_66), .in_65(y31), .y0_merged(out_9),
    .out_67(out_10), .out_68(out_11), .out_69(out_12), .out_70(out_13), .out_71(out_14), .out_72(out_15),
    .out_73(out_16), .out_74(out_17), .out_75(out_18), .out_76(out_19), .out_77(out_20), .out_78(out_21),
    .out_79(out_22), .out_80(out_23), .out_81(out_24), .out_82(out_25), .out_83(out_26), .out_84(out_27),
    .out_85(out_28), .out_86(out_29), .out_87(out_30), .out_88(out_31), .out_89(out_32), .out_90(out_33),
    .out_91(out_34), .out_92(out_35), .out_93(out_36), .out_94(out_37), .out_95(out_38), .out_96(out_39),
    .out_97(out_40), .in_1(op_code));
  draw_memory draw_memory_1 (
    .save(save), .reset(or_1_out), .in_3(y0), .in_4(y1), .in_5(y2), .in_6(y3), .in_7(y4), .in_8(y5),
    .in_9(y6), .in_10(y7), .in_11(y8), .in_12(y9), .in_13(y10), .in_14(y11), .in_15(y12), .in_16(y13),
    .in_17(y14), .in_18(y15), .in_19(y16), .in_20(y17), .in_21(y18), .in_22(y19), .in_23(y20), .in_24(y21),
    .in_25(y22), .in_26(y23), .in_27(y24), .in_28(y25), .in_29(y26), .in_30(y27), .in_31(y28), .in_32(y29),
    .in_33(y30), .in_34(y31), .out_35(draw_memory_1_out_35), .out_36(draw_memory_1_out_36),
    .out_37(draw_memory_1_out_37), .out_38(draw_memory_1_out_38), .out_39(draw_memory_1_out_39),
    .out_40(draw_memory_1_out_40), .out_41(draw_memory_1_out_41), .out_42(draw_memory_1_out_42),
    .out_43(draw_memory_1_out_43), .out_44(draw_memory_1_out_44), .out_45(draw_memory_1_out_45),
    .out_46(draw_memory_1_out_46), .out_47(draw_memory_1_out_47), .out_48(draw_memory_1_out_48),
    .out_49(draw_memory_1_out_49), .out_50(draw_memory_1_out_50), .out_51(draw_memory_1_out_51),
    .out_52(draw_memory_1_out_52), .out_53(draw_memory_1_out_53), .out_54(draw_memory_1_out_54),
    .out_55(draw_memory_1_out_55), .out_56(draw_memory_1_out_56), .out_57(draw_memory_1_out_57),
    .out_58(draw_memory_1_out_58), .out_59(draw_memory_1_out_59), .out_60(draw_memory_1_out_60),
    .out_61(draw_memory_1_out_61), .out_62(draw_memory_1_out_62), .out_63(draw_memory_1_out_63),
    .out_64(draw_memory_1_out_64), .out_65(draw_memory_1_out_65), .out_66(draw_memory_1_out_66));
  or or_1 (or_1_out, cancella, reset);
  xy_selector xy_selector_1 (
    .x(x), .y(y), .x16_output(y16), .CLK(clock), .x17_output(y17), .x18_output(y18), .x19_output(y19),
    .x20_output(y20), .x21_output(y21), .x22_output(y22), .x23_output(y23), .x24_output(y24),
    .x25_output(y25), .x26_output(y26), .x27_output(y27), .x28_output(y28), .x29_output(y29),
    .x30_output(y30), .x31_output(y31), .x0_output(y0), .x1_output(y1), .x2_output(y2), .x3_output(y3),
    .x4_output(y4), .x5_output(y5), .x6_output(y6), .x7_output(y7), .x8_output(y8), .x9_output(y9),
    .x10_output(y10), .x11_output(y11), .x12_output(y12), .x13_output(y13), .x14_output(y14),
    .x15_output(y15), .of(of), .Reset(reset));
endmodule

module m_op_code_displayer (
  input  [1:0] op_code,
  output [2:0] out_2,
  output [2:0] out_3,
  output [2:0] out_4
);

  Multiplexer #(.select(2), .width(3)) multiplexer_1 (
    .in0(3'b000), .in1(3'b111), .in2(3'b010), .out(out_3), .sel(op_code));  // open: in3, en

  assign out_2 = 3'b010;
  assign out_4 = 3'b010;
endmodule

module m_selection_displayer (
  input  [1:0] select,
  output out_2,
  output out_3,
  output out_4
);

  Demultiplexer #(.select(2)) demultiplexer_1 (
    .out0(out_2), .out1(out_3), .out2(out_4), .in(1'b1), .sel(select));  // open: out3, en
endmodule
