// Logisim project progetto.circ as structural Verilog: 10 circuits, main circuit main
module main (
  output [4:0] out_1,
  output [4:0] out_2,
  output [4:0] out_3,
  output [4:0] out_4
);

  wire _0_out, _1_out, _2_out, _3_out, _4_out, _5_out, _6_out, _7_out, _8_out, _9_out, Azzera, button_out,
       Clock, keypad_1_clicked, of, OK_out, or_1_out, or_2_out, or_3_out, Reset, save;
  wire [1:0] counter_1_q;
  wire [3:0] keypad_1_b0;
  wire [4:0] calcolo_1_out_5, X, Y;
  wire [31:0] merger_1_out_66, merger_1_out_67, merger_1_out_68, merger_1_out_69, merger_1_out_70,
       merger_1_out_71, merger_1_out_72, merger_1_out_73, merger_1_out_74, merger_1_out_75, merger_1_out_76,
       merger_1_out_77, merger_1_out_78, merger_1_out_79, merger_1_out_80, merger_1_out_81, merger_1_out_82,
       merger_1_out_83, merger_1_out_84, merger_1_out_85, merger_1_out_86, merger_1_out_87, merger_1_out_88,
       merger_1_out_89, merger_1_out_90, merger_1_out_91, merger_1_out_92, merger_1_out_93, merger_1_out_94,
       merger_1_out_95, merger_1_out_96, merger_1_y0_merged, xy_memory_1_out_35, xy_memory_1_out_36,
       xy_memory_1_out_37, xy_memory_1_out_38, xy_memory_1_out_39, xy_memory_1_out_40, xy_memory_1_out_41,
       xy_memory_1_out_42, xy_memory_1_out_43, xy_memory_1_out_44, xy_memory_1_out_45, xy_memory_1_out_46,
       xy_memory_1_out_47, xy_memory_1_out_48, xy_memory_1_out_49, xy_memory_1_out_50, xy_memory_1_out_51,
       xy_memory_1_out_52, xy_memory_1_out_53, xy_memory_1_out_54, xy_memory_1_out_55, xy_memory_1_out_56,
       xy_memory_1_out_57, xy_memory_1_out_58, xy_memory_1_out_59, xy_memory_1_out_60, xy_memory_1_out_61,
       xy_memory_1_out_62, xy_memory_1_out_63, xy_memory_1_out_64, xy_memory_1_out_65, xy_memory_1_out_66,
       y0, y1, y2, y3, y4, y5, y6, y7, y8, y9, y10, y11, y12, y13, y14, y15, y16, y17, y18, y19, y20, y21,
       y22, y23, y24, y25, y26, y27, y28, y29, y30, y31;

  Button R (.out(Reset));
  Button _8 (.out(_8_out));
  Button _7 (.out(_7_out));
  Button _4 (.out(_4_out));
  Button _5 (.out(_5_out));
  Button _1 (.out(_1_out));
  Button _2 (.out(_2_out));
  Button _0 (.out(_0_out));
  Button u_azzera (.out(Azzera));
  Button OK (.out(OK_out));
  Button u_save (.out(save));
  Button button (.out(button_out));
  DotMatrix #(.matrixcols(32), .matrixrows(32)) dotmatrix_1 (
    .col0(merger_1_y0_merged), .col1(merger_1_out_66), .col2(merger_1_out_67), .col3(merger_1_out_68),
    .col4(merger_1_out_69), .col5(merger_1_out_70), .col6(merger_1_out_71), .col7(merger_1_out_72),
    .col8(merger_1_out_73), .col9(merger_1_out_74), .col10(merger_1_out_75), .col11(merger_1_out_76),
    .col12(merger_1_out_77), .col13(merger_1_out_78), .col14(merger_1_out_79), .col15(merger_1_out_80),
    .col16(merger_1_out_81), .col17(merger_1_out_82), .col18(merger_1_out_83), .col19(merger_1_out_84),
    .col20(merger_1_out_85), .col21(merger_1_out_86), .col22(merger_1_out_87), .col23(merger_1_out_88),
    .col24(merger_1_out_89), .col25(merger_1_out_90), .col26(merger_1_out_91), .col27(merger_1_out_92),
    .col28(merger_1_out_93), .col29(merger_1_out_94), .col30(merger_1_out_95), .col31(merger_1_out_96));
  merger merger_1 (
    .y0_saved(xy_memory_1_out_35), .y0(y0), .in_3(xy_memory_1_out_36), .in_4(y1), .in_5(xy_memory_1_out_37),
    .in_6(y2), .in_7(xy_memory_1_out_38), .in_8(y3), .in_9(xy_memory_1_out_39), .in_10(y4),
    .in_11(xy_memory_1_out_40), .in_12(y5), .in_13(xy_memory_1_out_41), .in_14(y6),
    .in_15(xy_memory_1_out_42), .in_16(y7), .in_17(xy_memory_1_out_43), .in_18(y8),
    .in_19(xy_memory_1_out_44), .in_20(y9), .in_21(xy_memory_1_out_45), .errore_qui(y10),
    .in_23(xy_memory_1_out_46), .in_24(y11), .in_25(xy_memory_1_out_47), .in_26(y12),
    .in_27(xy_memory_1_out_48), .in_28(y13), .in_29(xy_memory_1_out_49), .in_30(y14),
    .in_31(xy_memory_1_out_50), .in_32(y15), .in_33(xy_memory_1_out_51), .in_34(y16),
    .in_35(xy_memory_1_out_52), .in_36(y17), .in_37(xy_memory_1_out_53), .in_38(y18),
    .in_39(xy_memory_1_out_54), .in_40(y19), .in_41(xy_memory_1_out_55), .in_42(y20),
    .in_43(xy_memory_1_out_56), .in_44(y21), .in_45(xy_memory_1_out_57), .in_46(y22),
    .in_47(xy_memory_1_out_58), .in_48(y23), .in_49(xy_memory_1_out_59), .in_50(y24),
    .in_51(xy_memory_1_out_60), .in_52(y25), .in_53(xy_memory_1_out_61), .in_54(y26),
    .in_55(xy_memory_1_out_62), .in_56(y27), .in_57(xy_memory_1_out_63), .in_58(y28),
    .in_59(xy_memory_1_out_64), .in_60(y29), .in_61(xy_memory_1_out_65), .in_62(y30),
    .in_63(xy_memory_1_out_66), .in_64(y31), .y0_merged(merger_1_y0_merged), .out_66(merger_1_out_66),
    .out_67(merger_1_out_67), .out_68(merger_1_out_68), .out_69(merger_1_out_69), .out_70(merger_1_out_70),
    .out_71(merger_1_out_71), .out_72(merger_1_out_72), .out_73(merger_1_out_73), .out_74(merger_1_out_74),
    .out_75(merger_1_out_75), .out_76(merger_1_out_76), .out_77(merger_1_out_77), .out_78(merger_1_out_78),
    .out_79(merger_1_out_79), .out_80(merger_1_out_80), .out_81(merger_1_out_81), .out_82(merger_1_out_82),
    .out_83(merger_1_out_83), .out_84(merger_1_out_84), .out_85(merger_1_out_85), .out_86(merger_1_out_86),
    .out_87(merger_1_out_87), .out_88(merger_1_out_88), .out_89(merger_1_out_89), .out_90(merger_1_out_90),
    .out_91(merger_1_out_91), .out_92(merger_1_out_92), .out_93(merger_1_out_93), .out_94(merger_1_out_94),
    .out_95(merger_1_out_95), .out_96(merger_1_out_96));
  xy_memory xy_memory_1 (
    .save(save), .reset(Reset), .in_3(y0), .in_4(y1), .in_5(y2), .in_6(y3), .in_7(y4), .in_8(y5), .in_9(y6),
    .in_10(y7), .in_11(y8), .in_12(y9), .in_13(y10), .in_14(y11), .in_15(y12), .in_16(y13), .in_17(y14),
    .in_18(y15), .in_19(y16), .in_20(y17), .in_21(y18), .in_22(y19), .in_23(y20), .in_24(y21), .in_25(y22),
    .in_26(y23), .in_27(y24), .in_28(y25), .in_29(y26), .in_30(y27), .in_31(y28), .in_32(y29), .in_33(y30),
    .in_34(y31), .out_35(xy_memory_1_out_35), .out_36(xy_memory_1_out_36), .out_37(xy_memory_1_out_37),
    .out_38(xy_memory_1_out_38), .out_39(xy_memory_1_out_39), .out_40(xy_memory_1_out_40),
    .out_41(xy_memory_1_out_41), .out_42(xy_memory_1_out_42), .out_43(xy_memory_1_out_43),
    .out_44(xy_memory_1_out_44), .out_45(xy_memory_1_out_45), .out_46(xy_memory_1_out_46),
    .out_47(xy_memory_1_out_47), .out_48(xy_memory_1_out_48), .out_49(xy_memory_1_out_49),
    .out_50(xy_memory_1_out_50), .out_51(xy_memory_1_out_51), .out_52(xy_memory_1_out_52),
    .out_53(xy_memory_1_out_53), .out_54(xy_memory_1_out_54), .out_55(xy_memory_1_out_55),
    .out_56(xy_memory_1_out_56), .out_57(xy_memory_1_out_57), .out_58(xy_memory_1_out_58),
    .out_59(xy_memory_1_out_59), .out_60(xy_memory_1_out_60), .out_61(xy_memory_1_out_61),
    .out_62(xy_memory_1_out_62), .out_63(xy_memory_1_out_63), .out_64(xy_memory_1_out_64),
    .out_65(xy_memory_1_out_65), .out_66(xy_memory_1_out_66));
  Button _9 (.out(_9_out));
  Button _6 (.out(_6_out));
  Button _3 (.out(_3_out));
  or or_1 (or_1_out, OK_out, button_out);
  keypad keypad_1 (
    ._0(_0_out), ._1(_1_out), ._3(_3_out), ._2(_2_out), ._5(_5_out), ._4(_4_out), ._7(_7_out), ._6(_6_out),
    .b2_2(keypad_1_b0[2]), .b1(keypad_1_b0[1]), .b0(keypad_1_b0[0]), ._8(_8_out), ._9(_9_out),
    .b2(keypad_1_b0[3]), .clicked(keypad_1_clicked));
  Counter #(.width(2), .max('h2), .trigger("falling")) counter_1 (
    .Q(counter_1_q), .clk(or_1_out), .clr(or_2_out));  // open: load, D, count, carry
  or or_2 (or_2_out, Reset, Azzera);
  or or_3 (or_3_out, Azzera, Reset);
  Counter #(.width(5), .max('h1f)) u_X (.Q(X), .clk(Clock), .clr(Reset));  // open: load, D, count, carry
  Clock CLK (.out(Clock));
  memory memory_1 (
    .in_1({1'b0, keypad_1_b0}), .in_2(keypad_1_clicked), .in_3(OK_out), .in_4(counter_1_q), .out_6(out_1),
    .out_7(out_2), .out_8(out_3), .out_9(out_4), .Reset(or_3_out));
  xy_selector xy_selector_1 (
    .x(X), .y(Y), .x16_output(y16), .CLK(Clock), .x17_output(y17), .x18_output(y18), .x19_output(y19),
    .x20_output(y20), .x21_output(y21), .x22_output(y22), .x23_output(y23), .x24_output(y24),
    .x25_output(y25), .x26_output(y26), .x27_output(y27), .x28_output(y28), .x29_output(y29),
    .x30_output(y30), .x31_output(y31), .x0_output(y0), .x1_output(y1), .x2_output(y2), .x3_output(y3),
    .x4_output(y4), .x5_output(y5), .x6_output(y6), .x7_output(y7), .x8_output(y8), .x9_output(y9),
    .x10_output(y10), .x11_output(y11), .x12_output(y12), .x13_output(y13), .x14_output(y14),
    .x15_output(y15), .of(of), .Reset(Reset));
  calcolo calcolo_1 (.c_x_2(out_1), .c_x(out_2), .q(out_3), .out_5(calcolo_1_out_5), .x(X), .out_6(of));
  assign Y = calcolo_1_out_5 & ~{5{of}};  // AND_Gate and_1, 5 bits wide
endmodule

module keypad (
  input  _0,
  input  _1,
  input  _3,
  input  _2,
  input  _5,
  input  _4,
  input  _7,
  input  _6,
  input  _9,
  input  _8,
  output clicked,
  output b2,
  output b2_2,
  output b1,
  output b0
);

  or or_1 (b0, _1, _9, _3, _5, _7);
  or or_2 (b1, _3, _2, _7, _6);
  or or_3 (b2_2, _6, _5, _7, _4);
  or or_4 (b2, _9, _8);
  or or_5 (clicked, _0, b0, b1, b2_2, b2);
endmodule

module negativator (
  input  [4:0] in_1,
  output [4:0] out_2
);

  wire [4:0] not_1_out;

  assign not_1_out = ~in_1;  // NOT_Gate not_1, 5 bits wide
  Adder #(.width(5)) adder_1 (.a(not_1_out), .b(5'b00001), .out(out_2));  // open: cin, cout
endmodule

module memory (
  input  [4:0] in_1,
  input  in_2,
  input  in_3,
  input  [1:0] in_4,
  input  Reset,
  output [4:0] out_6,
  output [4:0] out_7,
  output [4:0] out_8,
  output [4:0] out_9
);

  wire demultiplexer_2_out0, demultiplexer_2_out1, demultiplexer_2_out2, demultiplexer_2_out3;
  wire [4:0] d_ff_1_q, demultiplexer_1_out0, demultiplexer_1_out1, demultiplexer_1_out2, demultiplexer_1_out3;

  D_Flip_Flop d_ff_1 (.clk(in_2), .D(in_1[0]), .Q(d_ff_1_q[0]));  // open: Qn, preset, en, reset
  D_Flip_Flop d_ff_2 (.clk(in_2), .D(in_1[1]), .Q(d_ff_1_q[1]));  // open: Qn, preset, en, reset
  D_Flip_Flop d_ff_3 (.clk(in_2), .D(in_1[2]), .Q(d_ff_1_q[2]));  // open: Qn, preset, en, reset
  D_Flip_Flop d_ff_4 (.clk(in_2), .D(in_1[3]), .Q(d_ff_1_q[3]));  // open: Qn, preset, en, reset
  D_Flip_Flop d_ff_5 (.clk(in_2), .D(in_1[4]), .Q(d_ff_1_q[4]));  // open: Qn, preset, en, reset
  Demultiplexer #(.select(2), .width(5)) demultiplexer_1 (
    .out0(demultiplexer_1_out0), .out1(demultiplexer_1_out1), .out2(demultiplexer_1_out2),
    .out3(demultiplexer_1_out3), .in(d_ff_1_q), .sel(in_4));  // open: en
  Demultiplexer #(.select(2)) demultiplexer_2 (
    .out0(demultiplexer_2_out0), .out1(demultiplexer_2_out1), .out2(demultiplexer_2_out2),
    .out3(demultiplexer_2_out3), .in(in_3), .sel(in_4));  // open: en
  Register #(.width(5), .trigger("high")) register_1 (
    .D(demultiplexer_1_out0), .Q(out_6), .clk(demultiplexer_2_out0), .clr(Reset));  // open: en
  Register #(.width(5), .trigger("high")) register_2 (
    .D(demultiplexer_1_out1), .Q(out_7), .clk(demultiplexer_2_out1), .clr(Reset));  // open: en
  Register #(.width(5), .trigger("high")) register_3 (
    .D(demultiplexer_1_out2), .Q(out_8), .clk(demultiplexer_2_out2), .clr(Reset));  // open: en
  Register #(.width(5), .trigger("high")) register_4 (
    .D(demultiplexer_1_out3), .Q(out_9), .clk(demultiplexer_2_out3), .clr(Reset));  // open: en
endmodule

module minus (
  input  in_1,
  output out_2
);

  wire and_1_out, d_ff_1_qn;

  and and_1 (and_1_out, in_1, d_ff_1_qn);
  D_Flip_Flop #(.trigger("falling")) d_ff_1 (
    .clk(in_1), .D(and_1_out), .Q(out_2), .Qn(d_ff_1_qn));  // open: preset, en, reset
endmodule

module calcolo (
  input  [4:0] c_x_2,
  input  [4:0] c_x,
  input  [4:0] q,
  input  [4:0] x,
  output [4:0] out_5,
  output out_6
);

  wire adder_1_cout, adder_2_cout;
  wire [4:0] adder_1_out, multiplier_1_cout, multiplier_1_out, multiplier_2_cout, multiplier_2_out,
       multiplier_3_cout, multiplier_3_out;

  Multiplier #(.width(5)) multiplier_1 (.a(c_x), .b(x), .out(multiplier_1_out), .cout(multiplier_1_cout));  // open: cin
  Multiplier #(.width(5)) multiplier_2 (
    .a(c_x_2), .b(x), .out(multiplier_2_out), .cout(multiplier_2_cout));  // open: cin
  Multiplier #(.width(5)) multiplier_3 (
    .a(multiplier_2_out), .b(x), .out(multiplier_3_out), .cout(multiplier_3_cout));  // open: cin
  Adder #(.width(5)) adder_1 (
    .a(multiplier_3_out), .b(multiplier_1_out), .out(adder_1_out), .cout(adder_1_cout));  // open: cin
  Adder #(.width(5)) adder_2 (.a(q), .b(adder_1_out), .out(out_5), .cin(adder_1_cout), .cout(adder_2_cout));
  or or_1 (out_6, adder_1_cout, adder_2_cout, multiplier_3_cout[0], multiplier_3_cout[1], multiplier_3_cout[2], multiplier_3_cout[3], multiplier_3_cout[4], multiplier_1_cout[0], multiplier_1_cout[1], multiplier_1_cout[2], multiplier_1_cout[3], multiplier_1_cout[4], multiplier_2_cout[0], multiplier_2_cout[1], multiplier_2_cout[2], multiplier_2_cout[3], multiplier_2_cout[4]);
endmodule

module x_selector (
  input  [4:0] y,
  input  [4:0] x,
  input  CLK
);

  wire [4:0] dmx0, dmx1, dmx2, dmx3, dmx4, dmx5, dmx6, dmx7, dmx8, dmx9, dmx10, dmx11, dmx12, dmx13, dmx14,
       dmx15, dmx16, dmx17, dmx18, dmx19, dmx20, dmx21, dmx22, dmx23, dmx24, dmx25, dmx26, dmx27, dmx28,
       dmx29, dmx30, dmx31;
  wire [31:0] decoder_1_out0;

  Decoder #(.select(5)) decoder_1 (
    .out0(decoder_1_out0[0]), .out1(decoder_1_out0[1]), .out2(decoder_1_out0[2]), .out3(decoder_1_out0[3]),
    .out4(decoder_1_out0[4]), .out5(decoder_1_out0[5]), .out6(decoder_1_out0[6]), .out7(decoder_1_out0[7]),
    .out8(decoder_1_out0[8]), .out9(decoder_1_out0[9]), .out10(decoder_1_out0[10]),
    .out11(decoder_1_out0[11]), .out12(decoder_1_out0[12]), .out13(decoder_1_out0[13]),
    .out14(decoder_1_out0[14]), .out15(decoder_1_out0[15]), .out16(decoder_1_out0[16]),
    .out17(decoder_1_out0[17]), .out18(decoder_1_out0[18]), .out19(decoder_1_out0[19]),
    .out20(decoder_1_out0[20]), .out21(decoder_1_out0[21]), .out22(decoder_1_out0[22]),
    .out23(decoder_1_out0[23]), .out24(decoder_1_out0[24]), .out25(decoder_1_out0[25]),
    .out26(decoder_1_out0[26]), .out27(decoder_1_out0[27]), .out28(decoder_1_out0[28]),
    .out29(decoder_1_out0[29]), .out30(decoder_1_out0[30]), .out31(decoder_1_out0[31]), .sel(dmx0));  // open: en
  Demultiplexer #(.select(5), .width(5)) demultiplexer_1 (
    .out0(dmx0), .out1(dmx1), .out2(dmx2), .out3(dmx3), .out4(dmx4), .out5(dmx5), .out6(dmx6), .out7(dmx7),
    .out8(dmx8), .out9(dmx9), .out10(dmx10), .out11(dmx11), .out12(dmx12), .out13(dmx13), .out14(dmx14),
    .out15(dmx15), .out16(dmx16), .out17(dmx17), .out18(dmx18), .out19(dmx19), .out20(dmx20), .out21(dmx21),
    .out22(dmx22), .out23(dmx23), .out24(dmx24), .out25(dmx25), .out26(dmx26), .out27(dmx27), .out28(dmx28),
    .out29(dmx29), .out30(dmx30), .out31(dmx31), .in(y), .sel(x));  // open: en
endmodule

module xy_selector (
  input  [4:0] x,
  input  [4:0] y,
  input  CLK,
  input  Reset,
  input  of,
  output [31:0] x0_output,
  output [31:0] x16_output,
  output [31:0] x1_output,
  output [31:0] x17_output,
  output [31:0] x2_output,
  output [31:0] x18_output,
  output [31:0] x3_output,
  output [31:0] x19_output,
  output [31:0] x4_output,
  output [31:0] x20_output,
  output [31:0] x5_output,
  output [31:0] x21_output,
  output [31:0] x6_output,
  output [31:0] x22_output,
  output [31:0] x7_output,
  output [31:0] x23_output,
  output [31:0] x8_output,
  output [31:0] x24_output,
  output [31:0] x9_output,
  output [31:0] x25_output,
  output [31:0] x10_output,
  output [31:0] x26_output,
  output [31:0] x11_output,
  output [31:0] x27_output,
  output [31:0] x12_output,
  output [31:0] x28_output,
  output [31:0] x13_output,
  output [31:0] x29_output,
  output [31:0] x14_output,
  output [31:0] x30_output,
  output [31:0] x15_output,
  output [31:0] x31_output
);

  wire and_2_out, and_3_out, and_4_out, and_5_out, and_6_out, and_7_out, and_8_out, and_9_out, and_10_out,
       and_11_out, and_12_out, and_13_out, and_14_out, and_15_out, and_16_out, and_17_out, and_18_out,
       and_19_out, and_20_out, and_21_out, and_22_out, and_23_out, and_24_out, and_25_out, and_26_out,
       and_27_out, and_28_out, and_29_out, and_30_out, and_31_out, and_32_out, and_33_out;
  wire [31:0] y_star, y_t;

  assign y_star = ~{32{of}} & y_t;  // AND_Gate and_1, 32 bits wide
  Decoder #(.select(5)) decoder_1 (
    .out0(y_t[0]), .out1(y_t[1]), .out2(y_t[2]), .out3(y_t[3]), .out4(y_t[4]), .out5(y_t[5]), .out6(y_t[6]),
    .out7(y_t[7]), .out8(y_t[8]), .out9(y_t[9]), .out10(y_t[10]), .out11(y_t[11]), .out12(y_t[12]),
    .out13(y_t[13]), .out14(y_t[14]), .out15(y_t[15]), .out16(y_t[16]), .out17(y_t[17]), .out18(y_t[18]),
    .out19(y_t[19]), .out20(y_t[20]), .out21(y_t[21]), .out22(y_t[22]), .out23(y_t[23]), .out24(y_t[24]),
    .out25(y_t[25]), .out26(y_t[26]), .out27(y_t[27]), .out28(y_t[28]), .out29(y_t[29]), .out30(y_t[30]),
    .out31(y_t[31]), .sel(y));  // open: en
  Register #(.width(32), .trigger("high")) x16 (.D(y_star), .Q(x16_output), .clk(and_2_out), .clr(Reset));  // open: en
  and and_2 (and_2_out, x[4], ~x[3], ~x[2], ~x[1], ~x[0], CLK);  // AND_Gate
  Register #(.width(32), .trigger("high")) x17 (.D(y_star), .Q(x17_output), .clk(and_3_out), .clr(Reset));  // open: en
  and and_3 (and_3_out, x[4], ~x[3], ~x[2], ~x[1], x[0], CLK);  // AND_Gate
  Register #(.width(32), .trigger("high")) x18 (.D(y_star), .Q(x18_output), .clk(and_4_out), .clr(Reset));  // open: en
  and and_4 (and_4_out, x[4], ~x[3], ~x[2], x[1], ~x[0], CLK);  // AND_Gate
  Register #(.width(32), .trigger("high")) x19 (.D(y_star), .Q(x19_output), .clk(and_5_out), .clr(Reset));  // open: en
  and and_5 (and_5_out, x[4], ~x[3], ~x[2], x[1], x[0], CLK);  // AND_Gate
  Register #(.width(32), .trigger("high")) x20 (.D(y_star), .Q(x20_output), .clk(and_6_out), .clr(Reset));  // open: en
  and and_6 (and_6_out, x[4], ~x[3], x[2], ~x[1], ~x[0], CLK);  // AND_Gate
  Register #(.width(32), .trigger("high")) x21 (.D(y_star), .Q(x21_output), .clk(and_7_out), .clr(Reset));  // open: en
  and and_7 (and_7_out, x[4], ~x[3], x[2], ~x[1], x[0], CLK);  // AND_Gate
  Register #(.width(32), .trigger("high")) x22 (.D(y_star), .Q(x22_output), .clk(and_8_out), .clr(Reset));  // open: en
  and and_8 (and_8_out, x[4], ~x[3], x[2], x[1], ~x[0], CLK);  // AND_Gate
  Register #(.width(32), .trigger("high")) x23 (.D(y_star), .Q(x23_output), .clk(and_9_out), .clr(Reset));  // open: en
  and and_9 (and_9_out, x[4], ~x[3], x[2], x[1], x[0], CLK);  // AND_Gate
  Register #(.width(32), .trigger("high")) x24 (.D(y_star), .Q(x24_output), .clk(and_10_out), .clr(Reset));  // open: en
  and and_10 (and_10_out, x[4], x[3], ~x[2], ~x[1], ~x[0], CLK);  // AND_Gate
  Register #(.width(32), .trigger("high")) x25 (.D(y_star), .Q(x25_output), .clk(and_11_out), .clr(Reset));  // open: en
  and and_11 (and_11_out, x[4], x[3], ~x[2], ~x[1], x[0], CLK);  // AND_Gate
  Register #(.width(32), .trigger("high")) x26 (.D(y_star), .Q(x26_output), .clk(and_12_out), .clr(Reset));  // open: en
  and and_12 (and_12_out, x[4], x[3], ~x[2], x[1], ~x[0], CLK);  // AND_Gate
  Register #(.width(32), .trigger("high")) x27 (.D(y_star), .Q(x27_output), .clk(and_13_out), .clr(Reset));  // open: en
  and and_13 (and_13_out, x[4], x[3], ~x[2], x[1], x[0], CLK);  // AND_Gate
  Register #(.width(32), .trigger("high")) x28 (.D(y_star), .Q(x28_output), .clk(and_14_out), .clr(Reset));  // open: en
  and and_14 (and_14_out, x[4], x[3], x[2], ~x[1], ~x[0], CLK);  // AND_Gate
  Register #(.width(32), .trigger("high")) x29 (.D(y_star), .Q(x29_output), .clk(and_15_out), .clr(Reset));  // open: en
  and and_15 (and_15_out, x[4], x[3], x[2], ~x[1], x[0], CLK);  // AND_Gate
  Register #(.width(32), .trigger("high")) x30 (.D(y_star), .Q(x30_output), .clk(and_16_out), .clr(Reset));  // open: en
  and and_16 (and_16_out, x[4], x[3], x[2], x[1], ~x[0], CLK);  // AND_Gate
  Register #(.width(32), .trigger("high")) x31 (.D(y_star), .Q(x31_output), .clk(and_17_out), .clr(Reset));  // open: en
  and and_17 (and_17_out, x[4], x[3], x[2], x[1], x[0], CLK);
  Register #(.width(32), .trigger("high")) x0 (.D(y_star), .Q(x0_output), .clk(and_18_out), .clr(Reset));  // open: en
  and and_18 (and_18_out, ~x[4], ~x[3], ~x[2], ~x[1], ~x[0], CLK);  // AND_Gate
  Register #(.width(32), .trigger("high")) x1 (.D(y_star), .Q(x1_output), .clk(and_19_out), .clr(Reset));  // open: en
  and and_19 (and_19_out, ~x[4], ~x[3], ~x[2], ~x[1], x[0], CLK);  // AND_Gate
  Register #(.width(32), .trigger("high")) x2 (.D(y_star), .Q(x2_output), .clk(and_20_out), .clr(Reset));  // open: en
  and and_20 (and_20_out, ~x[4], ~x[3], ~x[2], x[1], ~x[0], CLK);  // AND_Gate
  Register #(.width(32), .trigger("high")) x3 (.D(y_star), .Q(x3_output), .clk(and_21_out), .clr(Reset));  // open: en
  and and_21 (and_21_out, ~x[4], ~x[3], ~x[2], x[1], x[0], CLK);  // AND_Gate
  Register #(.width(32), .trigger("high")) x4 (.D(y_star), .Q(x4_output), .clk(and_22_out), .clr(Reset));  // open: en
  and and_22 (and_22_out, ~x[4], ~x[3], x[2], ~x[1], ~x[0], CLK);  // AND_Gate
  Register #(.width(32), .trigger("high")) x5 (.D(y_star), .Q(x5_output), .clk(and_23_out), .clr(Reset));  // open: en
  and and_23 (and_23_out, ~x[4], ~x[3], x[2], ~x[1], x[0], CLK);  // AND_Gate
  Register #(.width(32), .trigger("high")) x6 (.D(y_star), .Q(x6_output), .clk(and_24_out), .clr(Reset));  // open: en
  and and_24 (and_24_out, ~x[4], ~x[3], x[2], x[1], ~x[0], CLK);  // AND_Gate
  Register #(.width(32), .trigger("high")) x7 (.D(y_star), .Q(x7_output), .clk(and_25_out), .clr(Reset));  // open: en
  and and_25 (and_25_out, ~x[4], ~x[3], x[2], x[1], x[0], CLK);  // AND_Gate
  Register #(.width(32), .trigger("high")) x8 (.D(y_star), .Q(x8_output), .clk(and_26_out), .clr(Reset));  // open: en
  and and_26 (and_26_out, ~x[4], x[3], ~x[2], ~x[1], ~x[0], CLK);  // AND_Gate
  Register #(.width(32), .trigger("high")) x9 (.D(y_star), .Q(x9_output), .clk(and_27_out), .clr(Reset));  // open: en
  and and_27 (and_27_out, ~x[4], x[3], ~x[2], ~x[1], x[0], CLK);  // AND_Gate
  Register #(.width(32), .trigger("high")) x10 (.D(y_star), .Q(x10_output), .clk(and_28_out), .clr(Reset));  // open: en
  and and_28 (and_28_out, ~x[4], x[3], ~x[2], x[1], ~x[0], CLK);  // AND_Gate
  Register #(.width(32), .trigger("high")) x11 (.D(y_star), .Q(x11_output), .clk(and_29_out), .clr(Reset));  // open: en
  and and_29 (and_29_out, ~x[4], x[3], ~x[2], x[1], x[0], CLK);  // AND_Gate
  Register #(.width(32), .trigger("high")) x12 (.D(y_star), .Q(x12_output), .clk(and_30_out), .clr(Reset));  // open: en
  and and_30 (and_30_out, ~x[4], x[3], x[2], ~x[1], ~x[0], CLK);  // AND_Gate
  Register #(.width(32), .trigger("high")) x13 (.D(y_star), .Q(x13_output), .clk(and_31_out), .clr(Reset));  // open: en
  and and_31 (and_31_out, ~x[4], x[3], x[2], ~x[1], x[0], CLK);  // AND_Gate
  Register #(.width(32), .trigger("high")) x14 (.D(y_star), .Q(x14_output), .clk(and_32_out), .clr(Reset));  // open: en
  and and_32 (and_32_out, ~x[4], x[3], x[2], x[1], ~x[0], CLK);  // AND_Gate
  Register #(.width(32), .trigger("high")) x15 (.D(y_star), .Q(x15_output), .clk(and_33_out), .clr(Reset));  // open: en
  and and_33 (and_33_out, ~x[4], x[3], x[2], x[1], x[0], CLK);  // AND_Gate
endmodule

module xy_memory (
  input  save,
  input  reset,
  input  [31:0] in_3,
  input  [31:0] in_4,
  input  [31:0] in_5,
  input  [31:0] in_6,
  input  [31:0] in_7,
  input  [31:0] in_8,
  input  [31:0] in_9,
  input  [31:0] in_10,
  input  [31:0] in_11,
  input  [31:0] in_12,
  input  [31:0] in_13,
  input  [31:0] in_14,
  input  [31:0] in_15,
  input  [31:0] in_16,
  input  [31:0] in_17,
  input  [31:0] in_18,
  input  [31:0] in_19,
  input  [31:0] in_20,
  input  [31:0] in_21,
  input  [31:0] in_22,
  input  [31:0] in_23,
  input  [31:0] in_24,
  input  [31:0] in_25,
  input  [31:0] in_26,
  input  [31:0] in_27,
  input  [31:0] in_28,
  input  [31:0] in_29,
  input  [31:0] in_30,
  input  [31:0] in_31,
  input  [31:0] in_32,
  input  [31:0] in_33,
  input  [31:0] in_34,
  output [31:0] out_35,
  output [31:0] out_36,
  output [31:0] out_37,
  output [31:0] out_38,
  output [31:0] out_39,
  output [31:0] out_40,
  output [31:0] out_41,
  output [31:0] out_42,
  output [31:0] out_43,
  output [31:0] out_44,
  output [31:0] out_45,
  output [31:0] out_46,
  output [31:0] out_47,
  output [31:0] out_48,
  output [31:0] out_49,
  output [31:0] out_50,
  output [31:0] out_51,
  output [31:0] out_52,
  output [31:0] out_53,
  output [31:0] out_54,
  output [31:0] out_55,
  output [31:0] out_56,
  output [31:0] out_57,
  output [31:0] out_58,
  output [31:0] out_59,
  output [31:0] out_60,
  output [31:0] out_61,
  output [31:0] out_62,
  output [31:0] out_63,
  output [31:0] out_64,
  output [31:0] out_65,
  output [31:0] out_66
);

  Register #(.width(32)) register_1 (.D(in_3), .Q(out_35), .clk(save), .clr(reset));  // open: en
  Register #(.width(32)) register_2 (.D(in_4), .Q(out_36), .clk(save), .clr(reset));  // open: en
  Register #(.width(32)) register_3 (.D(in_5), .Q(out_37), .clk(save), .clr(reset));  // open: en
  Register #(.width(32)) register_4 (.D(in_6), .Q(out_38), .clk(save), .clr(reset));  // open: en
  Register #(.width(32)) register_5 (.D(in_7), .Q(out_39), .clk(save), .clr(reset));  // open: en
  Register #(.width(32)) register_6 (.D(in_8), .Q(out_40), .clk(save), .clr(reset));  // open: en
  Register #(.width(32)) register_7 (.D(in_9), .Q(out_41), .clk(save), .clr(reset));  // open: en
  Register #(.width(32)) register_8 (.D(in_10), .Q(out_42), .clk(save), .clr(reset));  // open: en
  Register #(.width(32)) register_9 (.D(in_11), .Q(out_43), .clk(save), .clr(reset));  // open: en
  Register #(.width(32)) register_10 (.D(in_12), .Q(out_44), .clk(save), .clr(reset));  // open: en
  Register #(.width(32)) register_11 (.D(in_13), .Q(out_45), .clk(save), .clr(reset));  // open: en
  Register #(.width(32)) register_12 (.D(in_14), .Q(out_46), .clk(save), .clr(reset));  // open: en
  Register #(.width(32)) register_13 (.D(in_15), .Q(out_47), .clk(save), .clr(reset));  // open: en
  Register #(.width(32)) register_14 (.D(in_16), .Q(out_48), .clk(save), .clr(reset));  // open: en
  Register #(.width(32)) register_15 (.D(in_17), .Q(out_49), .clk(save), .clr(reset));  // open: en
  Register #(.width(32)) register_16 (.D(in_18), .Q(out_50), .clk(save), .clr(reset));  // open: en
  Register #(.width(32)) register_17 (.D(in_19), .Q(out_51), .clk(save), .clr(reset));  // open: en
  Register #(.width(32)) register_18 (.D(in_20), .Q(out_52), .clk(save), .clr(reset));  // open: en
  Register #(.width(32)) register_19 (.D(in_21), .Q(out_53), .clk(save), .clr(reset));  // open: en
  Register #(.width(32)) register_20 (.D(in_22), .Q(out_54), .clk(save), .clr(reset));  // open: en
  Register #(.width(32)) register_21 (.D(in_23), .Q(out_55), .clk(save), .clr(reset));  // open: en
  Register #(.width(32)) register_22 (.D(in_24), .Q(out_56), .clk(save), .clr(reset));  // open: en
  Register #(.width(32)) register_23 (.D(in_25), .Q(out_57), .clk(save), .clr(reset));  // open: en
  Register #(.width(32)) register_24 (.D(in_26), .Q(out_58), .clk(save), .clr(reset));  // open: en
  Register #(.width(32)) register_25 (.D(in_27), .Q(out_59), .clk(save), .clr(reset));  // open: en
  Register #(.width(32)) register_26 (.D(in_28), .Q(out_60), .clk(save), .clr(reset));  // open: en
  Register #(.width(32)) register_27 (.D(in_29), .Q(out_61), .clk(save), .clr(reset));  // open: en
  Register #(.width(32)) register_28 (.D(in_30), .Q(out_62), .clk(save), .clr(reset));  // open: en
  Register #(.width(32)) register_29 (.D(in_31), .Q(out_63), .clk(save), .clr(reset));  // open: en
  Register #(.width(32)) register_30 (.D(in_32), .Q(out_64), .clk(save), .clr(reset));  // open: en
  Register #(.width(32)) register_31 (.D(in_33), .Q(out_65), .clk(save), .clr(reset));  // open: en
  Register #(.width(32)) register_32 (.D(in_34), .Q(out_66), .clk(save), .clr(reset));  // open: en
endmodule

module merger (
  input  [31:0] y0_saved,
  input  [31:0] y0,
  input  [31:0] in_3,
  input  [31:0] in_4,
  input  [31:0] in_5,
  input  [31:0] in_6,
  input  [31:0] in_7,
  input  [31:0] in_8,
  input  [31:0] in_9,
  input  [31:0] in_10,
  input  [31:0] in_11,
  input  [31:0] in_12,
  input  [31:0] in_13,
  input  [31:0] in_14,
  input  [31:0] in_15,
  input  [31:0] in_16,
  input  [31:0] in_17,
  input  [31:0] in_18,
  input  [31:0] in_19,
  input  [31:0] in_20,
  input  [31:0] in_21,
  input  [31:0] errore_qui,
  input  [31:0] in_23,
  input  [31:0] in_24,
  input  [31:0] in_25,
  input  [31:0] in_26,
  input  [31:0] in_27,
  input  [31:0] in_28,
  input  [31:0] in_29,
  input  [31:0] in_30,
  input  [31:0] in_31,
  input  [31:0] in_32,
  input  [31:0] in_33,
  input  [31:0] in_34,
  input  [31:0] in_35,
  input  [31:0] in_36,
  input  [31:0] in_37,
  input  [31:0] in_38,
  input  [31:0] in_39,
  input  [31:0] in_40,
  input  [31:0] in_41,
  input  [31:0] in_42,
  input  [31:0] in_43,
  input  [31:0] in_44,
  input  [31:0] in_45,
  input  [31:0] in_46,
  input  [31:0] in_47,
  input  [31:0] in_48,
  input  [31:0] in_49,
  input  [31:0] in_50,
  input  [31:0] in_51,
  input  [31:0] in_52,
  input  [31:0] in_53,
  input  [31:0] in_54,
  input  [31:0] in_55,
  input  [31:0] in_56,
  input  [31:0] in_57,
  input  [31:0] in_58,
  input  [31:0] in_59,
  input  [31:0] in_60,
  input  [31:0] in_61,
  input  [31:0] in_62,
  input  [31:0] in_63,
  input  [31:0] in_64,
  output [31:0] y0_merged,
  output [31:0] out_66,
  output [31:0] out_67,
  output [31:0] out_68,
  output [31:0] out_69,
  output [31:0] out_70,
  output [31:0] out_71,
  output [31:0] out_72,
  output [31:0] out_73,
  output [31:0] out_74,
  output [31:0] out_75,
  output [31:0] out_76,
  output [31:0] out_77,
  output [31:0] out_78,
  output [31:0] out_79,
  output [31:0] out_80,
  output [31:0] out_81,
  output [31:0] out_82,
  output [31:0] out_83,
  output [31:0] out_84,
  output [31:0] out_85,
  output [31:0] out_86,
  output [31:0] out_87,
  output [31:0] out_88,
  output [31:0] out_89,
  output [31:0] out_90,
  output [31:0] out_91,
  output [31:0] out_92,
  output [31:0] out_93,
  output [31:0] out_94,
  output [31:0] out_95,
  output [31:0] out_96
);

  assign y0_merged = y0_saved | y0;  // OR_Gate or_1, 32 bits wide
  assign out_66 = in_3 | in_4;  // OR_Gate or_2, 32 bits wide
  assign out_67 = in_5 | in_6;  // OR_Gate or_3, 32 bits wide
  assign out_68 = in_7 | in_8;  // OR_Gate or_4, 32 bits wide
  assign out_69 = in_9 | in_10;  // OR_Gate or_5, 32 bits wide
  assign out_70 = in_11 | in_12;  // OR_Gate or_6, 32 bits wide
  assign out_71 = in_13 | in_14;  // OR_Gate or_7, 32 bits wide
  assign out_72 = in_15 | in_16;  // OR_Gate or_8, 32 bits wide
  assign out_73 = in_17 | in_18;  // OR_Gate or_9, 32 bits wide
  assign out_74 = in_19 | in_20;  // OR_Gate or_10, 32 bits wide
  assign out_75 = in_21 | errore_qui;  // OR_Gate or_11, 32 bits wide
  assign out_76 = in_23 | in_24;  // OR_Gate or_12, 32 bits wide
  assign out_77 = in_25 | in_26;  // OR_Gate or_13, 32 bits wide
  assign out_78 = in_27 | in_28;  // OR_Gate or_14, 32 bits wide
  assign out_79 = in_29 | in_30;  // OR_Gate or_15, 32 bits wide
  assign out_80 = in_31 | in_32;  // OR_Gate or_16, 32 bits wide
  assign out_81 = in_33 | in_34;  // OR_Gate or_17, 32 bits wide
  assign out_82 = in_35 | in_36;  // OR_Gate or_18, 32 bits wide
  assign out_83 = in_37 | in_38;  // OR_Gate or_19, 32 bits wide
  assign out_84 = in_39 | in_40;  // OR_Gate or_20, 32 bits wide
  assign out_85 = in_41 | in_42;  // OR_Gate or_21, 32 bits wide
  assign out_86 = in_43 | in_44;  // OR_Gate or_22, 32 bits wide
  assign out_87 = in_45 | in_46;  // OR_Gate or_23, 32 bits wide
  assign out_88 = in_47 | in_48;  // OR_Gate or_24, 32 bits wide
  assign out_89 = in_49 | in_50;  // OR_Gate or_25, 32 bits wide
  assign out_90 = in_51 | in_52;  // OR_Gate or_26, 32 bits wide
  assign out_91 = in_53 | in_54;  // OR_Gate or_27, 32 bits wide
  assign out_92 = in_55 | in_56;  // OR_Gate or_28, 32 bits wide
  assign out_93 = in_57 | in_58;  // OR_Gate or_29, 32 bits wide
  assign out_94 = in_59 | in_60;  // OR_Gate or_30, 32 bits wide
  assign out_95 = in_61 | in_62;  // OR_Gate or_31, 32 bits wide
  assign out_96 = in_63 | in_64;  // OR_Gate or_32, 32 bits wide
endmodule
