// Logisim project registers.circ as structural Verilog: 3 circuits, main circuit latch S/C async
// true
module latch_S_C_async (
  input  S,
  input  C,
  output nQ,
  output Q
);

  nor nor_1 (nQ, S, Q);
  nor nor_2 (Q, nQ, C);
endmodule

module latch_S_R_sync (
  input  in_1,
  input  in_2,
  output out_3,
  output out_4
);

  wire and_1_out, and_2_out, clock_1_out;

  and and_1 (and_1_out, in_1, clock_1_out);
  Clock clock_1 (.out(clock_1_out));
  and and_2 (and_2_out, clock_1_out, in_2);
  latch_S_C_async latch_s_c_async_1 (.S(and_1_out), .C(and_2_out), .nQ(out_3), .Q(out_4));
endmodule

module latch_D_sync (
  output Q,
  output nQ
);
endmodule
